// Logisim project final_proj.circ as structural Verilog
module main (
  input  clr
);

  wire alu_1_ovf, and_1_out, and_2_out, and_3_out, and_4_out, and_5_out, blt, bne, bnet, brch,
       brch_predictor_1_brch_pred, brch_predictor_1_if_brch_inst, clk_out, comparator_1_eq, comparator_2_eq,
       comparator_3_eq, comparator_3_lt, db_byp_1_stall, DC1, den, fdpipe_1_ifbrchout, flush, hazad, jal,
       jrbyp, jrs, ldm, ldw, nand_1_out, not_1_out, not_2_out, not_3_out, not_5_out, not_6_out, not_7_out,
       not_8_out, not_9_out, not_10_out, or_2_out, or_3_out, or_4_out, or_7_out, or_8_out, or_11_out,
       or_12_out, ovf, pcen, PCnonen, rdMbyp, rdMbyp2, rdXbyp, rsMbyp, rsMbyp2, rstat, rsw_t, rsXbyp,
       setxonbrchm, setxonbrchx, stall, stall_1_pc_nonen, str, swbyp, w_e, Wbyp3, XC1, XC2, xmpipe_1_ovfout;
  wire [1:0] and_7_out, byp, byp2, DB1, DB2, jmp, or_5_out;
  wire [4:0] AOPD, AOPF, AOPM, AOPW, AOPX, multiplexer_5_out, multiplexer_6_out, multiplexer_7_out_2,
       multiplexer_12_out, multiplexer_18_out;
  wire [11:0] bit_extender_2_out, bit_extender_7_out;
  wire [16:0] ImmD, ImmX;
  wire [26:0] multiplexer_7_out;
  wire [31:0] _1_result, alu_1_out_8, bit_extender_1_out, bit_extender_3_out, bit_extender_4_out,
       bit_extender_5_out, bit_extender_8_out, bit_extender_9_out, bit_extender_10_out,
       brch_predictor_1_pc_pred, dxpipe_1_a_out, dxpipe_1_b_out, dxpipe_1_pc_out, fdpipe_1_pc_out, IRF, IRM,
       IRW, jr, ldonjr, multiplexer_1_out, multiplexer_2_out, multiplexer_3_out, multiplexer_4_out,
       multiplexer_8_out, multiplexer_9_out, multiplexer_10_out, multiplexer_13_out, multiplexer_14_out,
       multiplexer_15_out, multiplexer_16_out, multiplexer_19_out, multiplexer_20_out, multiplexer_21_out,
       multiplexer_22_out, multiplexer_23_out, mwpipe_1_d_out, mwpipe_1_o_out, n32_bit_compact_1_result,
       PC_output, ram_1_data, registerfile_1_readdata1, registerfile_1_readdata2, tgt, undriven,
       xmpipe_1_b_out, xmpipe_1_o_out;
  wire [31:17] IRD, IRX;

  Clock clk (.out(clk_out));
  Multiplexer #(.width(32), .enable("false")) multiplexer_1 (
    .in0(multiplexer_2_out), .in1(brch_predictor_1_pc_pred), .out(multiplexer_1_out), .sel(and_1_out));
  assign bit_extender_1_out = {{20{1'b0}}, bit_extender_2_out};  // Bit_Extender bit_extender_1
  ROM #(.addrWidth(12), .dataWidth(32)) rom_1 ();  // open: addr, data, sel
  register_32 PC (.clk(clk_out), .\input (multiplexer_1_out), .enable(pcen), .\output (PC_output), .reset(clr));
  _32_bit_compact _1 (.result(_1_result), .A(bit_extender_1_out), .B(32'h1), .sub(1'b0));  // open: ovf
  or or_1 (flush, brch, jmp[0], jmp[1]);
  Bit_Extender #(.in_width(32), .out_width(12)) bit_extender_2 (.in(PC_output), .out(bit_extender_2_out));
  Multiplexer #(.width(32), .enable("false")) multiplexer_2 (
    .in0(_1_result), .in1(multiplexer_3_out), .out(multiplexer_2_out), .sel(flush));
  and and_1 (and_1_out, brch_predictor_1_if_brch_inst, brch_predictor_1_brch_pred);
  ROM #(.addrWidth(12), .dataWidth(32)) rom_2 ();  // open: addr, data, sel
  brch_predictor brch_predictor_1 (
    .brch_update(and_2_out), .brch_taken(or_7_out), .pc1(_1_result), .isn({IRF[31:7], AOPF, IRF[1:0]}),
    .brch_pred(brch_predictor_1_brch_pred), .pc_pred(brch_predictor_1_pc_pred),
    .if_brch_inst(brch_predictor_1_if_brch_inst), .brch_update_pc(fdpipe_1_pc_out), .clk(clk_out),
    .reset(clr), .brch_update_inst({IRD, ImmD[16:7], AOPD, ImmD[1:0]}));  // open: pc_no_pred
  Multiplexer #(.width(32), .enable("false")) multiplexer_3 (
    .in0(multiplexer_8_out), .in1(ldonjr), .out(multiplexer_3_out), .sel(jrbyp));
  not not_1 (not_1_out, or_2_out);
  or or_2 (or_2_out, hazad, stall);
  ROM #(.addrWidth(12), .dataWidth(32)) rom_3 (
    .addr(bit_extender_2_out), .data({IRF[31:7], AOPF, IRF[1:0]}));  // open: sel
  and and_2 (and_2_out, not_1_out, or_4_out, or_11_out);
  Comparator #(.width(5)) comparator_1 (.a(IRD[31:27]), .b(5'b00010), .eq(comparator_1_eq));  // open: gt, lt
  Comparator #(.width(5)) comparator_2 (.a(IRD[31:27]), .b(5'b00110), .eq(comparator_2_eq));  // open: gt, lt
  or or_3 (or_3_out, hazad, stall);
  not not_2 (not_2_out, hazad);
  or or_4 (or_4_out, comparator_1_eq, comparator_2_eq);
  FDpipe fdpipe_1 (
    .PC_IN(_1_result), .IR_IN(multiplexer_4_out), .clk(clk_out), .IR_OUT({IRD, ImmD[16:7], AOPD, ImmD[1:0]}),
    .PC_OUT(fdpipe_1_pc_out), .en(den), .clr(clr), .ifbrchin(and_1_out), .TG_IN(brch_predictor_1_pc_pred),
    .ifbrchout(fdpipe_1_ifbrchout));  // open: TG_OUT
  Multiplexer #(.width(32), .enable("false")) multiplexer_4 (
    .in0({IRF[31:7], AOPF, IRF[1:0]}), .in1({32{1'b0}}), .out(multiplexer_4_out), .sel(flush));
  or or_5 (or_5_out[0], jal, rstat);
  and and_3 (and_3_out, rsw_t, not_2_out);
  Comparator #(.width(32)) comparator_3 (
    .a(jr), .b(multiplexer_10_out), .eq(comparator_3_eq), .lt(comparator_3_lt));  // open: gt
  or or_6 (or_5_out[1], and_3_out, rstat);
  not not_3 (not_3_out, clk_out);
  Multiplexer #(.width(5), .enable("false")) multiplexer_5 (
    .in0(IRD[21:17]), .in1({5{1'b0}}), .out(multiplexer_5_out), .sel(jrs));
  Multiplexer #(.select(2), .width(5), .enable("false")) multiplexer_6 (
    .in0(IRW[26:22]), .in1({5{1'b1}}), .in2(5'b11110), .in3(5'b11110), .out(multiplexer_6_out), .sel(or_5_out));
  Multiplexer #(.width(32), .enable("false")) multiplexer_7 (
    .in0({IRD, ImmD[16:7], AOPD, ImmD[1:0]}), .in1({32{1'b0}}),
    .out({multiplexer_7_out_2, multiplexer_7_out}), .sel(or_3_out));
  Multiplexer #(.select(2), .width(32), .enable("false")) multiplexer_8 (
    .in0(multiplexer_20_out), .in1(bit_extender_3_out), .in2(jr), .out(multiplexer_8_out), .sel(jmp));  // open: in3
  not not_4 (bnet, comparator_3_eq);
  Multiplexer #(.select(2), .width(32), .enable("false")) multiplexer_9 (
    .in0(multiplexer_23_out), .in1(fdpipe_1_pc_out), .in2(bit_extender_10_out), .in3(tgt),
    .out(multiplexer_9_out), .sel(or_5_out));
  Control control_1 (
    .opf(IRF[31:27]), .opd(IRD[31:27]), .opx(IRX[31:27]), .opm(IRM[31:27]), .opw(IRW[31:27]), .bne(bnet),
    .DC1(DC1), .XC2(XC2), .XC1(XC1), .jrs(jrs), .jmp(jmp), .w_e(w_e), .ldm(ldm), .str(str), .ldw(ldw),
    .jal(jal), .bne_2(bne), .blt(blt), .rsw(rsw_t), .rdm(IRM[26:22]), .rdd(IRD[26:22]), .jrbyp(jrbyp));
  and and_4 (and_4_out, bnet, bne);
  or or_7 (or_7_out, and_4_out, and_5_out);
  and and_5 (and_5_out, comparator_3_lt, blt);
  DXpipe dxpipe_1 (
    .PC_IN(fdpipe_1_pc_out), .A_IN(multiplexer_10_out), .B_IN(jr),
    .IR_IN({multiplexer_7_out_2, multiplexer_7_out}), .clk(clk_out), .PC_OUT(dxpipe_1_pc_out),
    .A_OUT(dxpipe_1_a_out), .B_OUT(dxpipe_1_b_out), .IR_OUT({IRX, ImmX[16:7], AOPX, ImmX[1:0]}), .en(1'b1),
    .clr(clr));
  Multiplexer #(.select(2), .width(32), .enable("false")) multiplexer_10 (
    .in0(registerfile_1_readdata1), .in1(multiplexer_19_out), .in2(multiplexer_21_out), .in3(ram_1_data),
    .out(multiplexer_10_out), .sel(DB1));
  RegisterFile registerfile_1 (
    .WriteData(multiplexer_9_out), .RegWriteEnable(w_e), .clk(not_3_out), .reset(clr),
    .ReadData2(registerfile_1_readdata2), .ReadReg2(multiplexer_12_out), .ReadReg1(multiplexer_5_out),
    .ReadData1(registerfile_1_readdata1), .WriteReg(multiplexer_6_out));
  Multiplexer #(.select(2), .width(32), .enable("false")) multiplexer_11 (
    .in0(registerfile_1_readdata2), .in1(multiplexer_19_out), .in2(multiplexer_21_out), .in3(ram_1_data),
    .out(jr), .sel(DB2));
  Multiplexer #(.select(2), .width(5), .enable("false")) multiplexer_12 (
    .in0(ImmD[16:12]), .in1(IRD[26:22]), .in2(5'b11110), .out(multiplexer_12_out), .sel({jrs, DC1}));  // open: in3
  assign bit_extender_3_out = {{5{1'b0}}, {IRD[26:17], ImmD[16:7], AOPD, ImmD[1:0]}};  // Bit_Extender bit_extender_3
  Hazard hazard_1 (
    .FDRS1(IRD[21:17]), .DXRD(IRX[26:22]), .XMRD(IRM[26:22]), .FDRS2(ImmD[16:12]), .out_8(hazad),
    .IRM({IRM[31:7], AOPM, IRM[1:0]}), .IRW({IRW[31:7], AOPW, IRW[1:0]}), .Dop(IRD[31:27]));
  or or_8 (or_8_out, hazad, stall);
  not not_5 (not_5_out, flush);
  Multiplexer #(.select(2), .width(32), .enable("false")) multiplexer_13 (
    .in0(dxpipe_1_a_out), .in1(xmpipe_1_o_out), .in2(multiplexer_23_out), .in3(ram_1_data),
    .out(multiplexer_13_out), .sel(byp));
  Multiplexer #(.select(2), .width(32), .enable("false")) multiplexer_14 (
    .in0(dxpipe_1_b_out), .in1(xmpipe_1_o_out), .in2(multiplexer_23_out), .in3(ram_1_data),
    .out(multiplexer_14_out), .sel(byp2));
  assign bit_extender_4_out = {{15{ImmX[16]}}, {ImmX[16:7], AOPX, ImmX[1:0]}};  // Bit_Extender bit_extender_4
  or or_9 (den, brch, not_6_out);
  not not_6 (not_6_out, or_8_out);
  assign bit_extender_5_out = {{15{ImmD[16]}}, {ImmD[16:7], AOPD, ImmD[1:0]}};  // Bit_Extender bit_extender_5
  nand nand_1 (nand_1_out, or_8_out, not_5_out);
  Multiplexer #(.width(32), .enable("false")) multiplexer_15 (
    .in0(multiplexer_14_out), .in1(bit_extender_4_out), .out(multiplexer_15_out), .sel(XC2));
  Multiplexer #(.width(32), .enable("false")) multiplexer_16 (
    .in0(dxpipe_1_b_out), .in1(multiplexer_23_out), .out(multiplexer_16_out), .sel(swbyp));
  _32_bit_compact u_32_bit_compact_1 (
    .result(n32_bit_compact_1_result), .A(bit_extender_5_out), .B(fdpipe_1_pc_out), .sub(1'b0));  // open: ovf
  not not_7 (not_7_out, fdpipe_1_ifbrchout);
  not not_8 (not_8_out, or_7_out);
  Bypass bypass_1 (
    .DXRS1(IRX[21:17]), .XMRD(IRM[26:22]), .MWRD(IRW[26:22]), .Mbyp1(byp[0]), .Wbyp(byp[1]), .Mbyp2(byp2[0]),
    .Wbyp2(byp2[1]), .DXRS2(ImmX[16:12]), .bypout(Wbyp3), .Xop(IRX[31:27]), .Mop(IRM[31:27]),
    .DRD(IRD[26:22]), .MRD(IRM[26:22]), .swbyp(swbyp), .XRD(IRX[26:22]), .WOp(IRW[31:27]));
  not not_9 (not_9_out, stall_1_pc_nonen);
  and and_6 (pcen, not_9_out, nand_1_out);
  Multiplexer #(.width(32), .enable("false")) multiplexer_17 (
    .in0(xmpipe_1_o_out), .in1(ram_1_data), .out(ldonjr), .sel(ldm));
  ALU alu_1 (
    .InputData1(multiplexer_13_out), .ALUop(multiplexer_18_out), .InputData2(multiplexer_15_out),
    .out_8(alu_1_out_8), .shift(ImmX[11:7]), .ovf(alu_1_ovf));  // open: BLT, BNE
  Multiplexer #(.width(5), .enable("false")) multiplexer_18 (
    .in0(AOPX), .in1({5{1'b0}}), .out(multiplexer_18_out), .sel(XC1));
  Multiplexer #(.width(32), .enable("false")) multiplexer_19 (
    .in0(alu_1_out_8), .in1(bit_extender_9_out), .out(multiplexer_19_out), .sel(setxonbrchx));
  Multiplexer #(.select(2), .width(32), .enable("false")) multiplexer_20 (
    .in1(n32_bit_compact_1_result), .in2(fdpipe_1_pc_out), .out(multiplexer_20_out), .sel(and_7_out));  // open: in0, in3
  and and_7 (and_7_out[0], or_7_out, not_7_out);
  and and_8 (and_7_out[1], not_8_out, fdpipe_1_ifbrchout);
  or or_10 (stall, PCnonen, db_byp_1_stall);
  or or_11 (or_11_out, and_7_out[0], and_7_out[1]);
  Stall stall_1 (
    .DXOp(IRX[31:27]), .FDRS1(IRD[21:17]), .FDRS2(ImmD[16:12]), .DXRD(IRX[26:22]), .FDOp(IRD[31:27]),
    .stall(PCnonen), .FOp(IRF[31:27]), .PC_nonen(stall_1_pc_nonen));
  Multiplexer #(.width(32), .enable("false")) multiplexer_21 (
    .in0(xmpipe_1_o_out), .in1(undriven), .out(multiplexer_21_out), .sel(setxonbrchm));
  XMpipe xmpipe_1 (
    .O_IN(alu_1_out_8), .B_IN(multiplexer_16_out), .IR_IN({IRX, ImmX[16:7], AOPX, ImmX[1:0]}), .clk(clk_out),
    .O_OUT(xmpipe_1_o_out), .B_OUT(xmpipe_1_b_out), .IR_OUT({IRM[31:7], AOPM, IRM[1:0]}), .en(1'b1),
    .clr(clr), .ovfin(alu_1_ovf), .ovfout(xmpipe_1_ovfout));
  Bit_Extender #(.in_width(32), .out_width(27)) bit_extender_6 (.in(undriven), .out({IRM[26:7], AOPM, IRM[1:0]}));
  Bit_Extender #(.in_width(32), .out_width(12)) bit_extender_7 (.in(xmpipe_1_o_out), .out(bit_extender_7_out));
  Multiplexer #(.width(32), .enable("false")) multiplexer_22 (
    .in0(xmpipe_1_b_out), .in1(multiplexer_23_out), .out(multiplexer_22_out), .sel(Wbyp3));
  or or_12 (or_12_out, blt, bne);
  and and_9 (brch, or_12_out, or_11_out);
  assign bit_extender_8_out = {{5{1'b0}}, {IRX[26:17], ImmX[16:7], AOPX, ImmX[1:0]}};  // Bit_Extender bit_extender_8
  not not_10 (not_10_out, clk_out);
  assign bit_extender_9_out = {{5{1'b0}}, {IRX[26:17], ImmX[16:7], AOPX, ImmX[1:0]}};  // Bit_Extender bit_extender_9
  RStatus rstatus_1 (
    .ALUOp(IRW[31:27]), .ovf(ovf), .OP(AOPW), .Target(bit_extender_8_out), .statuswrite(rstat), .writeout(tgt));
  RAM #(.addrWidth(12), .dataWidth(32), .bus("separate")) ram_1 (
    .addr(bit_extender_7_out), .din(multiplexer_22_out), .data(ram_1_data), .str(str), .clk(not_10_out),
    .ld(ldm), .clr(clr));  // open: sel
  or or_13 (DB1[0], rsXbyp, rsMbyp2);
  or or_14 (DB1[1], rsMbyp, rsMbyp2);
  MWpipe mwpipe_1 (
    .O_IN(xmpipe_1_o_out), .D_IN(ram_1_data), .IR_IN({IRM[31:7], AOPM, IRM[1:0]}), .clk(clk_out),
    .O_OUT(mwpipe_1_o_out), .D_OUT(mwpipe_1_d_out), .IR_OUT({IRW[31:7], AOPW, IRW[1:0]}), .en(1'b1),
    .clr(clr), .ovfin(xmpipe_1_ovfout), .ovfout(ovf));
  DB_byp db_byp_1 (
    .Dop(IRD[31:27]), .Mop(IRM[31:27]), .Xop(IRX[31:27]), .rdm(IRM[26:22]), .rdx(IRX[26:22]),
    .rdd(IRD[26:22]), .rsd(IRD[21:17]), .rdXbyp(rdXbyp), .stall(db_byp_1_stall), .rsXbyp(rsXbyp),
    .sextonbrchx(setxonbrchx), .rdMbyp(rdMbyp), .rsMbyp(rsMbyp), .rdMbyp2(rdMbyp2), .rsMbyp2(rsMbyp2),
    .sextonbrchm(setxonbrchm));
  Multiplexer #(.width(32), .enable("false")) multiplexer_23 (
    .in0(mwpipe_1_o_out), .in1(mwpipe_1_d_out), .out(multiplexer_23_out), .sel(ldw));
  assign bit_extender_10_out = {{5{1'b0}}, multiplexer_7_out};  // Bit_Extender bit_extender_10
  or or_15 (DB2[0], rdXbyp, rdMbyp2);
  or or_16 (DB2[1], rdMbyp2, rdMbyp);

  // Other names for the same wires on the sheet: IRF[6:2] = AOPF; IRW[6:2] = AOPW; ImmX[6:2] = AOPX;
  //   IRX[16:0] = {ImmX[16:7], AOPX, ImmX[1:0]}; TgTX[26:0] = {IRX[26:17], ImmX[16:7], AOPX, ImmX[1:0]};
  //   Wbyp = byp[1]; Wbyp2 = byp2[1]; LTBF[1:0] = IRF[1:0]; LTBW[1:0] = IRW[1:0]; LTBX[1:0] = ImmX[1:0];
  //   OPCD[4:0] = IRD[31:27]; OPCF[4:0] = IRF[31:27]; OPCM[4:0] = IRM[31:27]; OPCW[4:0] = IRW[31:27];
  //   OPCX[4:0] = IRX[31:27]; RDF[4:0] = IRF[26:22]; RDW[4:0] = IRW[26:22]; RDX[4:0] = IRX[26:22];
  //   RSF[4:0] = IRF[21:17]; RSW[4:0] = IRW[21:17]; RSX[4:0] = IRX[21:17]; RTF[4:0] = IRF[16:12];
  //   RTW[4:0] = IRW[16:12]; RTX[4:0] = ImmX[16:12]; SHMF[4:0] = IRF[11:7]; SHMW[4:0] = IRW[11:7];
  //   SHMX[4:0] = ImmX[11:7]; IRD[16:0] = {ImmD[16:7], AOPD, ImmD[1:0]}; LTBD[1:0] = ImmD[1:0];
  //   TgTD[26:0] = {IRD[26:17], ImmD[16:7], AOPD, ImmD[1:0]}; ImmD[6:2] = AOPD; SHMD[4:0] = ImmD[11:7];
  //   RTD[4:0] = ImmD[16:12]; RSD[4:0] = IRD[21:17]; RDD[4:0] = IRD[26:22]; LTBM[1:0] = IRM[1:0];
  //   TgTM[26:0] = {IRM[26:7], AOPM, IRM[1:0]}; IRM[6:2] = AOPM; SHMM[4:0] = IRM[11:7]; RTM[4:0] = IRM[16:12];
  //   RSM[4:0] = IRM[21:17]; RDM[4:0] = IRM[26:22]

  // Notes on the sheet:
  //   ALU
  //   contents of rom_1 (hex, n*v repeats v):
  //   28400001 28800004 c41000 1061004 1461008 186100c 2061010 2061110 2061114 38c20001 41c20001 11c2000f
  //   0 0 0 18000010 2f800001 b0000012 b0000015 0 0 a8000000 a8010000 2841ffff 2881ffff 1000028c 28c00001
  //   1041000 1041000 28000000 4*0 20000 20000 0 20000 20000 4*0 800000f
  //   Pipeline Reading
  //   Branching
  //   contents of rom_2 (hex, n*v repeats v):
  //   28400001 28800003 c20004 10c20003 10c40001 0 30c40001
  //   contents of rom_3 (hex, n*v repeats v):
  //   0 0 0 2842000a 28840006 28c6000c 2909fffb 1422008 184300c 30440001 800000d 29ce00c8 1041ffff
  //   29ce012c 1041ffff
  //   Update
  //   Logic
  //   Branching Logic
  //   $rd MUX
  //   $rs MUX
  //   Control
endmodule

module RegisterFile (
  input  [31:0] WriteData,
  input  RegWriteEnable,
  input  clk,
  input  reset,
  input  [4:0] ReadReg2,
  input  [4:0] WriteReg,
  input  [4:0] ReadReg1,
  output [31:0] ReadData2,
  output [31:0] ReadData1
);

  wire decoder_1_out0, decoder_1_out1, decoder_1_out2, decoder_1_out3, decoder_1_out4, decoder_1_out5,
       decoder_1_out6, decoder_1_out7, decoder_1_out8, decoder_1_out9, decoder_1_out10, decoder_1_out11,
       decoder_1_out12, decoder_1_out13, decoder_1_out14, decoder_1_out15, decoder_1_out16, decoder_1_out17,
       decoder_1_out18, decoder_1_out19, decoder_1_out20, decoder_1_out21, decoder_1_out22, decoder_1_out23,
       decoder_1_out24, decoder_1_out25, decoder_1_out26, decoder_1_out27, decoder_1_out28, decoder_1_out29,
       decoder_1_out30, decoder_1_out31, decoder_2_out0, decoder_2_out1, decoder_2_out2, decoder_2_out3,
       decoder_2_out4, decoder_2_out5, decoder_2_out6, decoder_2_out7, decoder_2_out8, decoder_2_out9,
       decoder_2_out10, decoder_2_out11, decoder_2_out12, decoder_2_out13, decoder_2_out14, decoder_2_out15,
       decoder_2_out16, decoder_2_out17, decoder_2_out18, decoder_2_out19, decoder_2_out20, decoder_2_out21,
       decoder_2_out22, decoder_2_out23, decoder_2_out24, decoder_2_out25, decoder_2_out26, decoder_2_out27,
       decoder_2_out28, decoder_2_out29, decoder_2_out30, decoder_2_out31, en0, en1, en2, en3, en4, en5, en6,
       en7, en8, en9, en10, en11, en12, en13, en14, en15, en16, en17, en18, en19, en20, en21, en22, en23,
       en24, en25, en26, en27, en28, en29, en30, en31;
  wire [4:0] multiplexer_1_out;
  wire [31:0] _0, _1, _2, _3, _4, _5, _6, _7, _8, _9, _10, _11, _12, _13, _14, _15, _16, _17, _18, _19, _20,
       _21, _22, _23, _24, _25, _26, _27, _28, _29, _30, _31;

  assign ReadData2 = decoder_1_out0 ? _0 : 32'bz;  // Controlled_Buffer controlled_buffer_1
  assign ReadData1 = decoder_2_out0 ? _0 : 32'bz;  // Controlled_Buffer controlled_buffer_2
  assign ReadData2 = decoder_1_out1 ? _1 : 32'bz;  // Controlled_Buffer controlled_buffer_3
  assign ReadData1 = decoder_2_out1 ? _1 : 32'bz;  // Controlled_Buffer controlled_buffer_4
  register_32 register_32_1 (.clk(clk), .\input (WriteData), .enable(1'b0), .\output (_0), .reset(reset));
  register_32 register_32_2 (.clk(clk), .\input (WriteData), .enable(en1), .\output (_1), .reset(reset));
  register_32 register_32_3 (.clk(clk), .\input (WriteData), .enable(en2), .\output (_2), .reset(reset));
  register_32 register_32_4 (.clk(clk), .\input (WriteData), .enable(en3), .\output (_3), .reset(reset));
  register_32 register_32_5 (.clk(clk), .\input (WriteData), .enable(en4), .\output (_4), .reset(reset));
  register_32 register_32_6 (.clk(clk), .\input (WriteData), .enable(en5), .\output (_5), .reset(reset));
  register_32 register_32_7 (.clk(clk), .\input (WriteData), .enable(en6), .\output (_6), .reset(reset));
  register_32 register_32_8 (.clk(clk), .\input (WriteData), .enable(en7), .\output (_7), .reset(reset));
  assign ReadData2 = decoder_1_out3 ? _3 : 32'bz;  // Controlled_Buffer controlled_buffer_5
  assign ReadData2 = decoder_1_out2 ? _2 : 32'bz;  // Controlled_Buffer controlled_buffer_6
  assign ReadData1 = decoder_2_out2 ? _2 : 32'bz;  // Controlled_Buffer controlled_buffer_7
  assign ReadData1 = decoder_2_out3 ? _3 : 32'bz;  // Controlled_Buffer controlled_buffer_8
  assign ReadData2 = decoder_1_out4 ? _4 : 32'bz;  // Controlled_Buffer controlled_buffer_9
  assign ReadData1 = decoder_2_out4 ? _4 : 32'bz;  // Controlled_Buffer controlled_buffer_10
  assign ReadData1 = decoder_2_out5 ? _5 : 32'bz;  // Controlled_Buffer controlled_buffer_11
  assign ReadData2 = decoder_1_out6 ? _6 : 32'bz;  // Controlled_Buffer controlled_buffer_12
  assign ReadData2 = decoder_1_out5 ? _5 : 32'bz;  // Controlled_Buffer controlled_buffer_13
  assign ReadData1 = decoder_2_out6 ? _6 : 32'bz;  // Controlled_Buffer controlled_buffer_14
  register_32 register_32_9 (.clk(clk), .\input (WriteData), .enable(en8), .\output (_8), .reset(reset));
  register_32 register_32_10 (.clk(clk), .\input (WriteData), .enable(en9), .\output (_9), .reset(reset));
  register_32 register_32_11 (.clk(clk), .\input (WriteData), .enable(en10), .\output (_10), .reset(reset));
  register_32 register_32_12 (.clk(clk), .\input (WriteData), .enable(en11), .\output (_11), .reset(reset));
  register_32 register_32_13 (.clk(clk), .\input (WriteData), .enable(en12), .\output (_12), .reset(reset));
  register_32 register_32_14 (.clk(clk), .\input (WriteData), .enable(en13), .\output (_13), .reset(reset));
  register_32 register_32_15 (.clk(clk), .\input (WriteData), .enable(en14), .\output (_14), .reset(reset));
  register_32 register_32_16 (.clk(clk), .\input (WriteData), .enable(en15), .\output (_15), .reset(reset));
  assign ReadData2 = decoder_1_out8 ? _8 : 32'bz;  // Controlled_Buffer controlled_buffer_15
  assign ReadData2 = decoder_1_out7 ? _7 : 32'bz;  // Controlled_Buffer controlled_buffer_16
  assign ReadData1 = decoder_2_out8 ? _8 : 32'bz;  // Controlled_Buffer controlled_buffer_17
  assign ReadData1 = decoder_2_out7 ? _7 : 32'bz;  // Controlled_Buffer controlled_buffer_18
  assign ReadData2 = decoder_1_out9 ? _9 : 32'bz;  // Controlled_Buffer controlled_buffer_19
  assign ReadData1 = decoder_2_out9 ? _9 : 32'bz;  // Controlled_Buffer controlled_buffer_20
  assign ReadData2 = decoder_1_out10 ? _10 : 32'bz;  // Controlled_Buffer controlled_buffer_21
  assign ReadData2 = decoder_1_out11 ? _11 : 32'bz;  // Controlled_Buffer controlled_buffer_22
  assign ReadData1 = decoder_2_out10 ? _10 : 32'bz;  // Controlled_Buffer controlled_buffer_23
  assign ReadData1 = decoder_2_out11 ? _11 : 32'bz;  // Controlled_Buffer controlled_buffer_24
  assign ReadData2 = decoder_1_out12 ? _12 : 32'bz;  // Controlled_Buffer controlled_buffer_25
  assign ReadData1 = decoder_2_out13 ? _13 : 32'bz;  // Controlled_Buffer controlled_buffer_26
  assign ReadData1 = decoder_2_out12 ? _12 : 32'bz;  // Controlled_Buffer controlled_buffer_27
  register_32 register_32_17 (.clk(clk), .\input (WriteData), .enable(en16), .\output (_16), .reset(reset));
  register_32 register_32_18 (.clk(clk), .\input (WriteData), .enable(en17), .\output (_17), .reset(reset));
  register_32 register_32_19 (.clk(clk), .\input (WriteData), .enable(en18), .\output (_18), .reset(reset));
  register_32 register_32_20 (.clk(clk), .\input (WriteData), .enable(en19), .\output (_19), .reset(reset));
  register_32 register_32_21 (.clk(clk), .\input (WriteData), .enable(en20), .\output (_20), .reset(reset));
  register_32 register_32_22 (.clk(clk), .\input (WriteData), .enable(en21), .\output (_21), .reset(reset));
  register_32 register_32_23 (.clk(clk), .\input (WriteData), .enable(en22), .\output (_22), .reset(reset));
  register_32 register_32_24 (.clk(clk), .\input (WriteData), .enable(en23), .\output (_23), .reset(reset));
  assign ReadData2 = decoder_1_out13 ? _13 : 32'bz;  // Controlled_Buffer controlled_buffer_28
  assign ReadData2 = decoder_1_out14 ? _14 : 32'bz;  // Controlled_Buffer controlled_buffer_29
  Decoder #(.select(5), .enable("false")) decoder_1 (
    .out0(decoder_1_out0), .out1(decoder_1_out1), .out2(decoder_1_out2), .out3(decoder_1_out3),
    .out4(decoder_1_out4), .out5(decoder_1_out5), .out6(decoder_1_out6), .out7(decoder_1_out7),
    .out8(decoder_1_out8), .out9(decoder_1_out9), .out10(decoder_1_out10), .out11(decoder_1_out11),
    .out12(decoder_1_out12), .out13(decoder_1_out13), .out14(decoder_1_out14), .out15(decoder_1_out15),
    .out16(decoder_1_out16), .out17(decoder_1_out17), .out18(decoder_1_out18), .out19(decoder_1_out19),
    .out20(decoder_1_out20), .out21(decoder_1_out21), .out22(decoder_1_out22), .out23(decoder_1_out23),
    .out24(decoder_1_out24), .out25(decoder_1_out25), .out26(decoder_1_out26), .out27(decoder_1_out27),
    .out28(decoder_1_out28), .out29(decoder_1_out29), .out30(decoder_1_out30), .out31(decoder_1_out31),
    .sel(ReadReg2));
  assign ReadData1 = decoder_2_out14 ? _14 : 32'bz;  // Controlled_Buffer controlled_buffer_30
  Decoder #(.select(5), .enable("false")) decoder_2 (
    .out0(decoder_2_out0), .out1(decoder_2_out1), .out2(decoder_2_out2), .out3(decoder_2_out3),
    .out4(decoder_2_out4), .out5(decoder_2_out5), .out6(decoder_2_out6), .out7(decoder_2_out7),
    .out8(decoder_2_out8), .out9(decoder_2_out9), .out10(decoder_2_out10), .out11(decoder_2_out11),
    .out12(decoder_2_out12), .out13(decoder_2_out13), .out14(decoder_2_out14), .out15(decoder_2_out15),
    .out16(decoder_2_out16), .out17(decoder_2_out17), .out18(decoder_2_out18), .out19(decoder_2_out19),
    .out20(decoder_2_out20), .out21(decoder_2_out21), .out22(decoder_2_out22), .out23(decoder_2_out23),
    .out24(decoder_2_out24), .out25(decoder_2_out25), .out26(decoder_2_out26), .out27(decoder_2_out27),
    .out28(decoder_2_out28), .out29(decoder_2_out29), .out30(decoder_2_out30), .out31(decoder_2_out31),
    .sel(ReadReg1));
  assign ReadData2 = decoder_1_out15 ? _15 : 32'bz;  // Controlled_Buffer controlled_buffer_31
  assign ReadData1 = decoder_2_out15 ? _15 : 32'bz;  // Controlled_Buffer controlled_buffer_32
  assign ReadData2 = decoder_1_out16 ? _16 : 32'bz;  // Controlled_Buffer controlled_buffer_33
  assign ReadData1 = decoder_2_out16 ? _16 : 32'bz;  // Controlled_Buffer controlled_buffer_34
  register_32 register_32_25 (.clk(clk), .\input (WriteData), .enable(en24), .\output (_24), .reset(reset));
  register_32 register_32_26 (.clk(clk), .\input (WriteData), .enable(en25), .\output (_25), .reset(reset));
  register_32 register_32_27 (.clk(clk), .\input (WriteData), .enable(en26), .\output (_26), .reset(reset));
  register_32 register_32_28 (.clk(clk), .\input (WriteData), .enable(en27), .\output (_27), .reset(reset));
  register_32 register_32_29 (.clk(clk), .\input (WriteData), .enable(en28), .\output (_28), .reset(reset));
  register_32 register_32_30 (.clk(clk), .\input (WriteData), .enable(en29), .\output (_29), .reset(reset));
  register_32 register_32_31 (.clk(clk), .\input (WriteData), .enable(en30), .\output (_30), .reset(reset));
  register_32 register_32_32 (.clk(clk), .\input (WriteData), .enable(en31), .\output (_31), .reset(reset));
  assign ReadData2 = decoder_1_out17 ? _17 : 32'bz;  // Controlled_Buffer controlled_buffer_35
  assign ReadData2 = decoder_1_out18 ? _18 : 32'bz;  // Controlled_Buffer controlled_buffer_36
  assign ReadData1 = decoder_2_out17 ? _17 : 32'bz;  // Controlled_Buffer controlled_buffer_37
  assign ReadData1 = decoder_2_out18 ? _18 : 32'bz;  // Controlled_Buffer controlled_buffer_38
  assign ReadData2 = decoder_1_out19 ? _19 : 32'bz;  // Controlled_Buffer controlled_buffer_39
  assign ReadData1 = decoder_2_out19 ? _19 : 32'bz;  // Controlled_Buffer controlled_buffer_40
  assign ReadData1 = decoder_2_out20 ? _20 : 32'bz;  // Controlled_Buffer controlled_buffer_41
  assign ReadData2 = decoder_1_out21 ? _21 : 32'bz;  // Controlled_Buffer controlled_buffer_42
  assign ReadData2 = decoder_1_out20 ? _20 : 32'bz;  // Controlled_Buffer controlled_buffer_43
  assign ReadData1 = decoder_2_out21 ? _21 : 32'bz;  // Controlled_Buffer controlled_buffer_44
  assign ReadData2 = decoder_1_out23 ? _23 : 32'bz;  // Controlled_Buffer controlled_buffer_45
  assign ReadData2 = decoder_1_out22 ? _22 : 32'bz;  // Controlled_Buffer controlled_buffer_46
  assign ReadData1 = decoder_2_out22 ? _22 : 32'bz;  // Controlled_Buffer controlled_buffer_47
  assign ReadData1 = decoder_2_out23 ? _23 : 32'bz;  // Controlled_Buffer controlled_buffer_48
  assign ReadData2 = decoder_1_out24 ? _24 : 32'bz;  // Controlled_Buffer controlled_buffer_49
  assign ReadData1 = decoder_2_out24 ? _24 : 32'bz;  // Controlled_Buffer controlled_buffer_50
  // Probe on _0
  // Probe on _1
  // Probe on _2
  // Probe on _3
  // Probe on _4
  // Probe on _5
  // Probe on _6
  // Probe on _7
  assign ReadData2 = decoder_1_out26 ? _26 : 32'bz;  // Controlled_Buffer controlled_buffer_51
  assign ReadData2 = decoder_1_out25 ? _25 : 32'bz;  // Controlled_Buffer controlled_buffer_52
  assign ReadData1 = decoder_2_out26 ? _26 : 32'bz;  // Controlled_Buffer controlled_buffer_53
  assign ReadData1 = decoder_2_out25 ? _25 : 32'bz;  // Controlled_Buffer controlled_buffer_54
  assign ReadData2 = decoder_1_out27 ? _27 : 32'bz;  // Controlled_Buffer controlled_buffer_55
  assign ReadData1 = decoder_2_out27 ? _27 : 32'bz;  // Controlled_Buffer controlled_buffer_56
  assign ReadData1 = decoder_2_out28 ? _28 : 32'bz;  // Controlled_Buffer controlled_buffer_57
  assign ReadData2 = decoder_1_out28 ? _28 : 32'bz;  // Controlled_Buffer controlled_buffer_58
  assign ReadData2 = decoder_1_out29 ? _29 : 32'bz;  // Controlled_Buffer controlled_buffer_59
  assign ReadData1 = decoder_2_out29 ? _29 : 32'bz;  // Controlled_Buffer controlled_buffer_60
  // Probe on _8
  // Probe on _9
  // Probe on _10
  // Probe on _11
  // Probe on _12
  // Probe on _13
  // Probe on _14
  // Probe on _15
  assign ReadData2 = decoder_1_out31 ? _31 : 32'bz;  // Controlled_Buffer controlled_buffer_61
  assign ReadData2 = decoder_1_out30 ? _30 : 32'bz;  // Controlled_Buffer controlled_buffer_62
  assign ReadData1 = decoder_2_out31 ? _31 : 32'bz;  // Controlled_Buffer controlled_buffer_63
  assign ReadData1 = decoder_2_out30 ? _30 : 32'bz;  // Controlled_Buffer controlled_buffer_64
  // Probe on _16
  // Probe on _17
  // Probe on _18
  // Probe on _19
  // Probe on _20
  // Probe on _21
  // Probe on _22
  // Probe on _23
  // Probe on _24
  // Probe on _25
  // Probe on _26
  // Probe on _27
  // Probe on _28
  // Probe on _29
  // Probe on _30
  // Probe on _31
  Multiplexer #(.width(5), .enable("false")) multiplexer_1 (
    .in0({5{1'b0}}), .in1(WriteReg), .out(multiplexer_1_out), .sel(RegWriteEnable));
  Decoder #(.select(5), .enable("false")) decoder_3 (
    .out0(en0), .out1(en1), .out2(en2), .out3(en3), .out4(en4), .out5(en5), .out6(en6), .out7(en7),
    .out8(en8), .out9(en9), .out10(en10), .out11(en11), .out12(en12), .out13(en13), .out14(en14),
    .out15(en15), .out16(en16), .out17(en17), .out18(en18), .out19(en19), .out20(en20), .out21(en21),
    .out22(en22), .out23(en23), .out24(en24), .out25(en25), .out26(en26), .out27(en27), .out28(en28),
    .out29(en29), .out30(en30), .out31(en31), .sel(multiplexer_1_out));

  // Other names for the same wires on the sheet: data[31:0] = WriteData; enab = RegWriteEnable
endmodule

module register_32 (
  input  enable,
  input  reset,
  input  clk,
  input  [31:0] \input ,
  output [31:0] \output 
);

  wire enable_t, not_1_out;

  not not_1 (not_1_out, clk);
  and and_1 (enable_t, not_1_out, enable);
  D_Flip_Flop d_ff_1 (.clk(clk), .D(\input [0]), .Q(\output [0]), .en(enable_t), .reset(reset));  // open: Qn, preset
  D_Flip_Flop d_ff_2 (.clk(clk), .D(\input [1]), .Q(\output [1]), .en(enable_t), .reset(reset));  // open: Qn, preset
  D_Flip_Flop d_ff_3 (.clk(clk), .D(\input [2]), .Q(\output [2]), .en(enable_t), .reset(reset));  // open: Qn, preset
  D_Flip_Flop d_ff_4 (.clk(clk), .D(\input [3]), .Q(\output [3]), .en(enable_t), .reset(reset));  // open: Qn, preset
  D_Flip_Flop d_ff_5 (.clk(clk), .D(\input [4]), .Q(\output [4]), .en(enable_t), .reset(reset));  // open: Qn, preset
  D_Flip_Flop d_ff_6 (.clk(clk), .D(\input [5]), .Q(\output [5]), .en(enable_t), .reset(reset));  // open: Qn, preset
  D_Flip_Flop d_ff_7 (.clk(clk), .D(\input [6]), .Q(\output [6]), .en(enable_t), .reset(reset));  // open: Qn, preset
  D_Flip_Flop d_ff_8 (.clk(clk), .D(\input [7]), .Q(\output [7]), .en(enable_t), .reset(reset));  // open: Qn, preset
  D_Flip_Flop d_ff_9 (.clk(clk), .D(\input [16]), .Q(\output [16]), .en(enable_t), .reset(reset));  // open: Qn, preset
  D_Flip_Flop d_ff_10 (.clk(clk), .D(\input [17]), .Q(\output [17]), .en(enable_t), .reset(reset));  // open: Qn, preset
  D_Flip_Flop d_ff_11 (.clk(clk), .D(\input [18]), .Q(\output [18]), .en(enable_t), .reset(reset));  // open: Qn, preset
  D_Flip_Flop d_ff_12 (.clk(clk), .D(\input [19]), .Q(\output [19]), .en(enable_t), .reset(reset));  // open: Qn, preset
  D_Flip_Flop d_ff_13 (.clk(clk), .D(\input [20]), .Q(\output [20]), .en(enable_t), .reset(reset));  // open: Qn, preset
  D_Flip_Flop d_ff_14 (.clk(clk), .D(\input [21]), .Q(\output [21]), .en(enable_t), .reset(reset));  // open: Qn, preset
  D_Flip_Flop d_ff_15 (.clk(clk), .D(\input [22]), .Q(\output [22]), .en(enable_t), .reset(reset));  // open: Qn, preset
  D_Flip_Flop d_ff_16 (.clk(clk), .D(\input [23]), .Q(\output [23]), .en(enable_t), .reset(reset));  // open: Qn, preset
  D_Flip_Flop d_ff_17 (.clk(clk), .D(\input [8]), .Q(\output [8]), .en(enable_t), .reset(reset));  // open: Qn, preset
  D_Flip_Flop d_ff_18 (.clk(clk), .D(\input [9]), .Q(\output [9]), .en(enable_t), .reset(reset));  // open: Qn, preset
  D_Flip_Flop d_ff_19 (.clk(clk), .D(\input [10]), .Q(\output [10]), .en(enable_t), .reset(reset));  // open: Qn, preset
  D_Flip_Flop d_ff_20 (.clk(clk), .D(\input [11]), .Q(\output [11]), .en(enable_t), .reset(reset));  // open: Qn, preset
  D_Flip_Flop d_ff_21 (.clk(clk), .D(\input [12]), .Q(\output [12]), .en(enable_t), .reset(reset));  // open: Qn, preset
  D_Flip_Flop d_ff_22 (.clk(clk), .D(\input [13]), .Q(\output [13]), .en(enable_t), .reset(reset));  // open: Qn, preset
  D_Flip_Flop d_ff_23 (.clk(clk), .D(\input [14]), .Q(\output [14]), .en(enable_t), .reset(reset));  // open: Qn, preset
  D_Flip_Flop d_ff_24 (.clk(clk), .D(\input [15]), .Q(\output [15]), .en(enable_t), .reset(reset));  // open: Qn, preset
  D_Flip_Flop d_ff_25 (.clk(clk), .D(\input [24]), .Q(\output [24]), .en(enable_t), .reset(reset));  // open: Qn, preset
  D_Flip_Flop d_ff_26 (.clk(clk), .D(\input [25]), .Q(\output [25]), .en(enable_t), .reset(reset));  // open: Qn, preset
  D_Flip_Flop d_ff_27 (.clk(clk), .D(\input [26]), .Q(\output [26]), .en(enable_t), .reset(reset));  // open: Qn, preset
  D_Flip_Flop d_ff_28 (.clk(clk), .D(\input [27]), .Q(\output [27]), .en(enable_t), .reset(reset));  // open: Qn, preset
  D_Flip_Flop d_ff_29 (.clk(clk), .D(\input [28]), .Q(\output [28]), .en(enable_t), .reset(reset));  // open: Qn, preset
  D_Flip_Flop d_ff_30 (.clk(clk), .D(\input [29]), .Q(\output [29]), .en(enable_t), .reset(reset));  // open: Qn, preset
  D_Flip_Flop d_ff_31 (.clk(clk), .D(\input [30]), .Q(\output [30]), .en(enable_t), .reset(reset));  // open: Qn, preset
  D_Flip_Flop d_ff_32 (.clk(clk), .D(\input [31]), .Q(\output [31]), .en(enable_t), .reset(reset));  // open: Qn, preset

  // Other names for the same wires on the sheet: first[7:0] = \input [7:0]; second[7:0] = \input [15:8];
  //   third[7:0] = \input [23:16]; fourth[7:0] = \input [31:24]
endmodule

module ALU (
  input  [4:0] shift,
  input  [31:0] InputData1,
  input  [31:0] InputData2,
  input  [4:0] ALUop,
  output ovf,
  output BNE,
  output BLT,
  output [31:0] out_8
);

  wire comparator_1_eq, n32_bit_compact_1_ovf, n32_bit_compact_2_ovf;
  wire [31:0] and_1_out, n32_bit_compact_1_result, n32_bit_compact_2_result, or_1_out, shifter_1_out,
       shifter_2_out;

  Shifter #(.width(32)) shifter_1 (.in(InputData1), .\dist (shift), .out(shifter_1_out));
  Shifter #(.width(32), .shift("ar")) shifter_2 (.in(InputData1), .\dist (shift), .out(shifter_2_out));
  _32_bit_compact u_32_bit_compact_1 (
    .result(n32_bit_compact_1_result), .A(InputData1), .B(InputData2), .ovf(n32_bit_compact_1_ovf), .sub(1'b0));
  _32_bit_compact u_32_bit_compact_2 (
    .result(n32_bit_compact_2_result), .A(InputData1), .B(InputData2), .ovf(n32_bit_compact_2_ovf), .sub(1'b1));
  assign and_1_out = InputData1 & InputData2;  // AND_Gate and_1, 32 bits wide
  assign or_1_out = InputData1 | InputData2;  // OR_Gate or_1, 32 bits wide
  or or_2 (ovf, n32_bit_compact_2_ovf, n32_bit_compact_1_ovf);
  Multiplexer #(.select(5), .width(32), .enable("false")) multiplexer_1 (
    .in0(n32_bit_compact_1_result), .in1(n32_bit_compact_2_result), .in2(and_1_out), .in3(or_1_out),
    .in4(shifter_1_out), .in5(shifter_2_out), .out(out_8), .sel(ALUop));  // open: in6, in7, in8, in9, in10, in11, in12, in13, in14, in15, in16, in17, in18, in19, in20, in21, in22, in23, in24, in25, in26, in27, in28, in29, in30, in31
  Comparator #(.width(32)) comparator_1 (.a(InputData1), .b(InputData2), .gt(BLT), .eq(comparator_1_eq));  // open: lt
  not not_1 (BNE, comparator_1_eq);

  // Other names for the same wires on the sheet: A[31:0] = InputData1; B[31:0] = InputData2
endmodule

module one_bit_add (
  input  cin,
  input  a,
  input  b,
  output cout,
  output sum
);

  wire and_1_out, and_2_out, xor_1_out;

  or or_1 (cout, and_1_out, and_2_out);
  xor xor_1 (xor_1_out, a, b);
  and and_1 (and_1_out, a, b);
  and and_2 (and_2_out, xor_1_out, cin);
  xor xor_2 (sum, cin, xor_1_out);
endmodule

module _32_bit_add (
  input  a31,
  input  b31,
  input  a30,
  input  b30,
  input  a29,
  input  b29,
  input  a28,
  input  b28,
  input  a27,
  input  b27,
  input  a26,
  input  b26,
  input  a25,
  input  b25,
  input  a24,
  input  b24,
  input  a23,
  input  b23,
  input  a22,
  input  b22,
  input  a21,
  input  b21,
  input  a20,
  input  b20,
  input  a19,
  input  b19,
  input  a18,
  input  b18,
  input  a17,
  input  b17,
  input  a16,
  input  b16,
  input  add_sub,
  input  a15,
  input  b15,
  input  a14,
  input  b14,
  input  a13,
  input  b13,
  input  a12,
  input  b12,
  input  a11,
  input  b11,
  input  a10,
  input  b10,
  input  a9,
  input  b9,
  input  a8,
  input  b8,
  input  a7,
  input  b7,
  input  a6,
  input  b6,
  input  a5,
  input  b5,
  input  a4,
  input  b4,
  input  a3,
  input  b3,
  input  a2,
  input  b2,
  input  a1,
  input  b1,
  input  a0,
  input  b0,
  output ovf,
  output s31,
  output s30,
  output s29,
  output s28,
  output s27,
  output s26,
  output s25,
  output s24,
  output cout,
  output s23,
  output s22,
  output s21,
  output s20,
  output s19,
  output s18,
  output s17,
  output s16,
  output s15,
  output s14,
  output s13,
  output s12,
  output s11,
  output s10,
  output s9,
  output s8,
  output s7,
  output s6,
  output s5,
  output s4,
  output s3,
  output s2,
  output s1,
  output s0
);

  wire one_bit_add_2_cout, one_bit_add_3_cout, one_bit_add_4_cout, one_bit_add_5_cout, one_bit_add_6_cout,
       one_bit_add_7_cout, one_bit_add_8_cout, one_bit_add_9_cout, one_bit_add_10_cout, one_bit_add_11_cout,
       one_bit_add_12_cout, one_bit_add_13_cout, one_bit_add_14_cout, one_bit_add_15_cout,
       one_bit_add_16_cout, one_bit_add_17_cout, one_bit_add_18_cout, one_bit_add_19_cout,
       one_bit_add_20_cout, one_bit_add_21_cout, one_bit_add_22_cout, one_bit_add_23_cout,
       one_bit_add_24_cout, one_bit_add_25_cout, one_bit_add_26_cout, one_bit_add_27_cout,
       one_bit_add_28_cout, one_bit_add_29_cout, one_bit_add_30_cout, one_bit_add_31_cout,
       one_bit_add_32_cout, xor_2_out, xor_3_out, xor_4_out, xor_5_out, xor_6_out, xor_7_out, xor_8_out,
       xor_9_out, xor_10_out, xor_11_out, xor_12_out, xor_13_out, xor_14_out, xor_15_out, xor_16_out,
       xor_17_out, xor_18_out, xor_19_out, xor_20_out, xor_21_out, xor_22_out, xor_23_out, xor_24_out,
       xor_25_out, xor_26_out, xor_27_out, xor_28_out, xor_29_out, xor_30_out, xor_31_out, xor_32_out,
       xor_33_out;

  xor xor_1 (ovf, cout, one_bit_add_5_cout);
  one_bit_add one_bit_add_1 (.a(a31), .b(xor_2_out), .cout(cout), .cin(one_bit_add_5_cout), .sum(s31));
  xor xor_2 (xor_2_out, add_sub, b31);
  one_bit_add one_bit_add_2 (.a(a23), .b(xor_3_out), .cout(one_bit_add_2_cout), .cin(one_bit_add_6_cout), .sum(s23));
  xor xor_3 (xor_3_out, add_sub, b23);
  one_bit_add one_bit_add_3 (.a(a15), .b(xor_4_out), .cout(one_bit_add_3_cout), .cin(one_bit_add_7_cout), .sum(s15));
  xor xor_4 (xor_4_out, add_sub, b15);
  one_bit_add one_bit_add_4 (.a(a7), .b(xor_5_out), .cout(one_bit_add_4_cout), .cin(one_bit_add_8_cout), .sum(s7));
  xor xor_5 (xor_5_out, add_sub, b7);
  one_bit_add one_bit_add_5 (.a(a30), .b(xor_6_out), .cout(one_bit_add_5_cout), .cin(one_bit_add_9_cout), .sum(s30));
  xor xor_6 (xor_6_out, add_sub, b30);
  one_bit_add one_bit_add_6 (.a(a22), .b(xor_7_out), .cout(one_bit_add_6_cout), .cin(one_bit_add_10_cout), .sum(s22));
  xor xor_7 (xor_7_out, add_sub, b22);
  one_bit_add one_bit_add_7 (.a(a14), .b(xor_8_out), .cout(one_bit_add_7_cout), .cin(one_bit_add_11_cout), .sum(s14));
  xor xor_8 (xor_8_out, add_sub, b14);
  one_bit_add one_bit_add_8 (.a(a6), .b(xor_9_out), .cout(one_bit_add_8_cout), .cin(one_bit_add_12_cout), .sum(s6));
  xor xor_9 (xor_9_out, add_sub, b6);
  one_bit_add one_bit_add_9 (.a(a29), .b(xor_10_out), .cout(one_bit_add_9_cout), .cin(one_bit_add_13_cout), .sum(s29));
  xor xor_10 (xor_10_out, add_sub, b29);
  one_bit_add one_bit_add_10 (
    .a(a21), .b(xor_11_out), .cout(one_bit_add_10_cout), .cin(one_bit_add_14_cout), .sum(s21));
  xor xor_11 (xor_11_out, add_sub, b21);
  one_bit_add one_bit_add_11 (
    .a(a13), .b(xor_12_out), .cout(one_bit_add_11_cout), .cin(one_bit_add_15_cout), .sum(s13));
  xor xor_12 (xor_12_out, add_sub, b13);
  one_bit_add one_bit_add_12 (.a(a5), .b(xor_13_out), .cout(one_bit_add_12_cout), .cin(one_bit_add_16_cout), .sum(s5));
  xor xor_13 (xor_13_out, add_sub, b5);
  one_bit_add one_bit_add_13 (
    .a(a28), .b(xor_14_out), .cout(one_bit_add_13_cout), .cin(one_bit_add_17_cout), .sum(s28));
  xor xor_14 (xor_14_out, add_sub, b28);
  one_bit_add one_bit_add_14 (
    .a(a20), .b(xor_15_out), .cout(one_bit_add_14_cout), .cin(one_bit_add_18_cout), .sum(s20));
  xor xor_15 (xor_15_out, add_sub, b20);
  one_bit_add one_bit_add_15 (
    .a(a12), .b(xor_16_out), .cout(one_bit_add_15_cout), .cin(one_bit_add_19_cout), .sum(s12));
  xor xor_16 (xor_16_out, add_sub, b12);
  one_bit_add one_bit_add_16 (.a(a4), .b(xor_17_out), .cout(one_bit_add_16_cout), .cin(one_bit_add_20_cout), .sum(s4));
  one_bit_add one_bit_add_17 (
    .a(a27), .b(xor_18_out), .cout(one_bit_add_17_cout), .cin(one_bit_add_21_cout), .sum(s27));
  one_bit_add one_bit_add_18 (
    .a(a19), .b(xor_19_out), .cout(one_bit_add_18_cout), .cin(one_bit_add_22_cout), .sum(s19));
  one_bit_add one_bit_add_19 (
    .a(a11), .b(xor_20_out), .cout(one_bit_add_19_cout), .cin(one_bit_add_23_cout), .sum(s11));
  one_bit_add one_bit_add_20 (.a(a3), .b(xor_21_out), .cout(one_bit_add_20_cout), .cin(one_bit_add_25_cout), .sum(s3));
  xor xor_17 (xor_17_out, add_sub, b4);
  one_bit_add one_bit_add_21 (
    .a(a26), .b(xor_22_out), .cout(one_bit_add_21_cout), .cin(one_bit_add_24_cout), .sum(s26));
  xor xor_18 (xor_18_out, add_sub, b27);
  one_bit_add one_bit_add_22 (
    .a(a18), .b(xor_23_out), .cout(one_bit_add_22_cout), .cin(one_bit_add_26_cout), .sum(s18));
  xor xor_19 (xor_19_out, add_sub, b19);
  one_bit_add one_bit_add_23 (
    .a(a10), .b(xor_24_out), .cout(one_bit_add_23_cout), .cin(one_bit_add_27_cout), .sum(s10));
  xor xor_20 (xor_20_out, add_sub, b11);
  xor xor_21 (xor_21_out, add_sub, b3);
  one_bit_add one_bit_add_24 (
    .a(a25), .b(xor_26_out), .cout(one_bit_add_24_cout), .cin(one_bit_add_29_cout), .sum(s25));
  xor xor_22 (xor_22_out, add_sub, b26);
  xor xor_23 (xor_23_out, add_sub, b18);
  xor xor_24 (xor_24_out, add_sub, b10);
  one_bit_add one_bit_add_25 (.a(a2), .b(xor_25_out), .cout(one_bit_add_25_cout), .cin(one_bit_add_28_cout), .sum(s2));
  xor xor_25 (xor_25_out, add_sub, b2);
  xor xor_26 (xor_26_out, add_sub, b25);
  one_bit_add one_bit_add_26 (
    .a(a17), .b(xor_27_out), .cout(one_bit_add_26_cout), .cin(one_bit_add_30_cout), .sum(s17));
  xor xor_27 (xor_27_out, add_sub, b17);
  one_bit_add one_bit_add_27 (.a(a9), .b(xor_28_out), .cout(one_bit_add_27_cout), .cin(one_bit_add_31_cout), .sum(s9));
  xor xor_28 (xor_28_out, add_sub, b9);
  one_bit_add one_bit_add_28 (.a(a1), .b(xor_29_out), .cout(one_bit_add_28_cout), .cin(one_bit_add_32_cout), .sum(s1));
  xor xor_29 (xor_29_out, add_sub, b1);
  one_bit_add one_bit_add_29 (.a(a24), .b(xor_30_out), .cout(one_bit_add_29_cout), .cin(one_bit_add_2_cout), .sum(s24));
  xor xor_30 (xor_30_out, add_sub, b24);
  one_bit_add one_bit_add_30 (.a(a16), .b(xor_31_out), .cout(one_bit_add_30_cout), .cin(one_bit_add_3_cout), .sum(s16));
  xor xor_31 (xor_31_out, add_sub, b16);
  one_bit_add one_bit_add_31 (.a(a8), .b(xor_32_out), .cout(one_bit_add_31_cout), .cin(one_bit_add_4_cout), .sum(s8));
  xor xor_32 (xor_32_out, add_sub, b8);
  one_bit_add one_bit_add_32 (.a(a0), .b(xor_33_out), .cout(one_bit_add_32_cout), .cin(add_sub), .sum(s0));
  xor xor_33 (xor_33_out, add_sub, b0);
endmodule

module _32_bit_compact (
  input  [31:0] A,
  input  [31:0] B,
  input  sub,
  output ovf,
  output [31:0] result
);

  _32_bit_add u_32_bit_add_1 (
    .add_sub(sub), .ovf(ovf), .s7(result[7]), .s31(result[31]), .s23(result[23]), .s15(result[15]),
    .s30(result[30]), .s22(result[22]), .s14(result[14]), .s6(result[6]), .s29(result[29]), .s21(result[21]),
    .s13(result[13]), .s5(result[5]), .s28(result[28]), .s20(result[20]), .s12(result[12]), .s4(result[4]),
    .s27(result[27]), .s19(result[19]), .s11(result[11]), .s3(result[3]), .s26(result[26]), .s18(result[18]),
    .s10(result[10]), .s2(result[2]), .s25(result[25]), .s17(result[17]), .s9(result[9]), .s1(result[1]),
    .s24(result[24]), .s16(result[16]), .s8(result[8]), .s0(result[0]), .a31(A[31]), .a23(A[23]),
    .a15(A[15]), .a7(A[7]), .b31(B[31]), .b23(B[23]), .b15(B[15]), .b7(B[7]), .a30(A[30]), .a22(A[22]),
    .a14(A[14]), .a6(A[6]), .b30(B[30]), .b22(B[22]), .b14(B[14]), .b6(B[6]), .a29(A[29]), .a21(A[21]),
    .a13(A[13]), .a5(A[5]), .b29(B[29]), .b21(B[21]), .b13(B[13]), .b5(B[5]), .a28(A[28]), .a20(A[20]),
    .a12(A[12]), .a4(A[4]), .b28(B[28]), .b20(B[20]), .b12(B[12]), .b4(B[4]), .a27(A[27]), .a19(A[19]),
    .a11(A[11]), .a3(A[3]), .b27(B[27]), .b19(B[19]), .b11(B[11]), .b3(B[3]), .a26(A[26]), .a18(A[18]),
    .a10(A[10]), .a2(A[2]), .b26(B[26]), .b18(B[18]), .b10(B[10]), .b2(B[2]), .a25(A[25]), .a17(A[17]),
    .a9(A[9]), .a1(A[1]), .b25(B[25]), .b17(B[17]), .b9(B[9]), .b1(B[1]), .a24(A[24]), .a16(A[16]),
    .a8(A[8]), .a0(A[0]), .b24(B[24]), .b16(B[16]), .b8(B[8]), .b0(B[0]));  // open: cout
endmodule

module FDpipe (
  input  [31:0] PC_IN,
  input  [31:0] IR_IN,
  input  clk,
  input  en,
  input  clr,
  input  ifbrchin,
  input  [31:0] TG_IN,
  output [31:0] PC_OUT,
  output [31:0] IR_OUT,
  output ifbrchout,
  output [31:0] TG_OUT
);

  register_32 register_32_1 (.clk(clk), .\input (PC_IN), .enable(en), .\output (PC_OUT), .reset(clr));
  register_32 register_32_2 (.clk(clk), .\input (IR_IN), .enable(en), .\output (IR_OUT), .reset(clr));
  D_Flip_Flop d_ff_1 (.clk(clk), .D(ifbrchin), .Q(ifbrchout), .en(en), .reset(clr));  // open: Qn, preset
  register_32 register_32_3 (.clk(clk), .\input (TG_IN), .enable(en), .\output (TG_OUT), .reset(clr));
endmodule

module DXpipe (
  input  [31:0] PC_IN,
  input  [31:0] A_IN,
  input  [31:0] B_IN,
  input  [31:0] IR_IN,
  input  clk,
  input  en,
  input  clr,
  output [31:0] PC_OUT,
  output [31:0] A_OUT,
  output [31:0] B_OUT,
  output [31:0] IR_OUT
);

  register_32 register_32_1 (.clk(clk), .\input (PC_IN), .enable(en), .\output (PC_OUT), .reset(clr));
  register_32 register_32_2 (.clk(clk), .\input (A_IN), .enable(en), .\output (A_OUT), .reset(clr));
  register_32 register_32_3 (.clk(clk), .\input (B_IN), .enable(en), .\output (B_OUT), .reset(clr));
  register_32 register_32_4 (.clk(clk), .\input (IR_IN), .enable(en), .\output (IR_OUT), .reset(clr));
endmodule

module XMpipe (
  input  [31:0] O_IN,
  input  [31:0] B_IN,
  input  [31:0] IR_IN,
  input  clk,
  input  en,
  input  clr,
  input  ovfin,
  output [31:0] O_OUT,
  output [31:0] B_OUT,
  output [31:0] IR_OUT,
  output ovfout
);

  register_32 register_32_1 (.clk(clk), .\input (O_IN), .enable(en), .\output (O_OUT), .reset(clr));
  register_32 register_32_2 (.clk(clk), .\input (B_IN), .enable(en), .\output (B_OUT), .reset(clr));
  register_32 register_32_3 (.clk(clk), .\input (IR_IN), .enable(en), .\output (IR_OUT), .reset(clr));
  D_Flip_Flop d_ff_1 (.clk(clk), .D(ovfin), .Q(ovfout), .en(en), .reset(clr));  // open: Qn, preset
endmodule

module MWpipe (
  input  [31:0] O_IN,
  input  [31:0] D_IN,
  input  [31:0] IR_IN,
  input  clk,
  input  en,
  input  clr,
  input  ovfin,
  output [31:0] O_OUT,
  output [31:0] D_OUT,
  output [31:0] IR_OUT,
  output ovfout
);

  register_32 register_32_1 (.clk(clk), .\input (O_IN), .enable(en), .\output (O_OUT), .reset(clr));
  register_32 register_32_2 (.clk(clk), .\input (D_IN), .enable(en), .\output (D_OUT), .reset(clr));
  register_32 register_32_3 (.clk(clk), .\input (IR_IN), .enable(en), .\output (IR_OUT), .reset(clr));
  D_Flip_Flop d_ff_1 (.clk(clk), .D(ovfin), .Q(ovfout), .en(en), .reset(clr));  // open: Qn, preset
endmodule

module Control (
  input  [4:0] opf,
  input  [4:0] opd,
  input  [4:0] opx,
  input  [4:0] opm,
  input  [4:0] opw,
  input  bne,
  input  [4:0] rdm,
  input  [4:0] rdd,
  output DC1,
  output XC2,
  output XC1,
  output jrs,
  output bne_2,
  output blt,
  output [1:0] jmp,
  output w_e,
  output jal,
  output rsw,
  output ldm,
  output str,
  output jrbyp,
  output ldw
);

  wire and_1_out, and_2_out, and_3_out, and_4_out, and_5_out, and_6_out, and_7_out, and_8_out, and_12_out,
       and_13_out, and_14_out, and_15_out, and_17_out, and_19_out, and_22_out, and_25_out, and_26_out,
       and_27_out, and_28_out, and_29_out, and_30_out, comparator_1_eq, comparator_2_eq, comparator_3_eq,
       not_1_out, not_2_out, not_3_out, not_4_out, not_5_out, not_6_out, not_7_out, not_8_out, not_9_out,
       not_10_out, not_11_out, not_12_out, not_13_out, not_14_out, not_15_out, not_16_out, not_17_out,
       not_18_out, not_19_out, not_20_out, not_21_out, not_22_out, not_23_out, not_24_out, not_25_out,
       not_26_out, not_27_out, not_28_out, not_29_out, not_30_out, not_31_out, not_32_out, not_33_out,
       not_34_out, not_35_out, not_36_out, not_37_out, not_38_out, not_39_out, not_40_out, not_41_out,
       not_42_out, not_43_out, not_44_out, not_45_out, not_46_out, not_47_out, not_48_out, not_49_out,
       not_50_out, not_51_out, not_52_out, not_53_out, not_54_out, not_55_out, not_56_out, not_57_out,
       not_58_out, not_59_out, not_60_out, not_61_out, not_62_out, not_63_out, not_64_out, not_65_out,
       not_66_out, not_67_out, not_68_out, not_69_out, not_70_out, not_71_out, not_72_out, not_73_out,
       not_74_out, not_75_out, not_76_out, not_77_out, not_78_out, not_79_out, not_80_out, not_81_out,
       not_82_out, not_83_out, not_84_out, not_85_out, not_86_out, not_87_out, not_88_out, not_89_out,
       not_90_out, not_91_out, not_92_out, not_93_out, not_94_out, not_95_out, not_96_out, or_5_out;

  not not_1 (not_1_out, opx[4]);
  not not_2 (not_2_out, opx[3]);
  not not_3 (not_3_out, opx[1]);
  not not_4 (not_4_out, opx[4]);
  not not_5 (not_5_out, opx[3]);
  not not_6 (not_6_out, opx[4]);
  not not_7 (not_7_out, opx[2]);
  not not_8 (not_8_out, opx[1]);
  not not_9 (not_9_out, opx[0]);
  not not_10 (not_10_out, opw[4]);
  not not_11 (not_11_out, opw[3]);
  not not_12 (not_12_out, opw[2]);
  not not_13 (not_13_out, opw[1]);
  not not_14 (not_14_out, opw[0]);
  not not_15 (not_15_out, opw[4]);
  not not_16 (not_16_out, opw[2]);
  not not_17 (not_17_out, opw[1]);
  not not_18 (not_18_out, opw[0]);
  not not_19 (not_19_out, opw[4]);
  not not_20 (not_20_out, opw[3]);
  not not_21 (not_21_out, opw[1]);
  not not_22 (not_22_out, opw[3]);
  not not_23 (not_23_out, opw[1]);
  not not_24 (not_24_out, opw[4]);
  not not_25 (not_25_out, opw[3]);
  not not_26 (not_26_out, opw[2]);
  and and_1 (and_1_out, not_1_out, not_2_out, opx[2], not_3_out, opx[0]);
  and and_2 (and_2_out, not_4_out, not_5_out, opx[2], opx[1], opx[0]);
  and and_3 (and_3_out, not_6_out, opx[3], not_7_out, not_8_out, not_9_out);
  and and_4 (and_4_out, not_10_out, not_11_out, not_12_out, not_13_out, not_14_out);
  and and_5 (and_5_out, not_15_out, opw[3], not_16_out, not_17_out, not_18_out);
  and and_6 (and_6_out, not_19_out, not_20_out, opw[2], not_21_out, opw[0]);
  and and_7 (and_7_out, opw[4], not_22_out, opw[2], not_23_out, opw[0]);
  and and_8 (and_8_out, not_24_out, not_25_out, not_26_out, opw[1], opw[0]);
  not not_27 (not_27_out, opm[4]);
  not not_28 (not_28_out, opm[2]);
  not not_29 (not_29_out, opm[1]);
  not not_30 (not_30_out, opm[0]);
  not not_31 (not_31_out, opm[4]);
  not not_32 (not_32_out, opm[3]);
  not not_33 (not_33_out, opw[4]);
  not not_34 (not_34_out, opw[2]);
  not not_35 (not_35_out, opw[1]);
  not not_36 (not_36_out, opw[0]);
  or or_1 (XC1, and_1_out, and_2_out, and_3_out);
  or or_2 (w_e, and_4_out, and_5_out, and_6_out, and_7_out, and_8_out);
  and and_9 (ldm, not_27_out, opm[3], not_28_out, not_29_out, not_30_out);
  and and_10 (str, not_31_out, not_32_out, opm[2], opm[1], opm[0]);
  and and_11 (ldw, not_33_out, opw[3], not_34_out, not_35_out, not_36_out);
  not not_37 (not_37_out, opd[4]);
  not not_38 (not_38_out, opd[3]);
  not not_39 (not_39_out, opd[1]);
  not not_40 (not_40_out, opd[0]);
  not not_41 (not_41_out, opd[3]);
  not not_42 (not_42_out, opd[1]);
  not not_43 (not_43_out, opd[4]);
  not not_44 (not_44_out, opd[3]);
  and and_12 (and_12_out, not_43_out, not_44_out, opd[2], opd[1], opd[0]);
  not not_45 (not_45_out, opd[4]);
  not not_46 (not_46_out, opd[3]);
  and and_13 (and_13_out, not_45_out, not_46_out, not_47_out, opd[1], not_48_out);
  not not_47 (not_47_out, opd[2]);
  not not_48 (not_48_out, opd[0]);
  not not_49 (not_49_out, opd[4]);
  not not_50 (not_50_out, opd[3]);
  and and_14 (and_14_out, not_49_out, not_50_out, opd[2], not_51_out, not_52_out);
  not not_51 (not_51_out, opd[1]);
  not not_52 (not_52_out, opd[0]);
  not not_53 (not_53_out, opd[4]);
  not not_54 (not_54_out, opd[3]);
  and and_15 (and_15_out, not_53_out, not_54_out, opd[2], opd[1], not_55_out);
  not not_55 (not_55_out, opd[0]);
  not not_56 (not_56_out, opd[3]);
  and and_16 (jrs, opd[4], not_56_out, opd[2], opd[1], not_57_out);
  not not_57 (not_57_out, opd[0]);
  not not_58 (not_58_out, opd[4]);
  not not_59 (not_59_out, opd[3]);
  not not_60 (not_60_out, opd[2]);
  and and_17 (and_17_out, not_58_out, not_59_out, not_60_out, not_61_out, opd[0]);
  not not_61 (not_61_out, opd[1]);
  not not_62 (not_62_out, opd[4]);
  not not_63 (not_63_out, opd[3]);
  and and_18 (jal, not_62_out, not_63_out, not_64_out, opd[1], opd[0]);
  not not_64 (not_64_out, opd[2]);
  not not_65 (not_65_out, opd[3]);
  and and_19 (and_19_out, opd[4], not_65_out, opd[2], opd[1], not_66_out);
  not not_66 (not_66_out, opd[0]);
  and and_20 (jmp[1], not_37_out, not_38_out, opd[2], not_39_out, not_40_out);
  and and_21 (rsw, opd[4], not_41_out, opd[2], not_42_out, opd[0]);
  or or_3 (jmp[0], and_17_out, jal, and_22_out);
  and and_22 (and_22_out, and_19_out, bne);
  or or_4 (DC1, and_12_out, and_13_out, and_14_out, and_15_out);
  not not_67 (not_67_out, opd[4]);
  not not_68 (not_68_out, opd[3]);
  not not_69 (not_69_out, opd[2]);
  not not_70 (not_70_out, opd[0]);
  not not_71 (not_71_out, opd[4]);
  not not_72 (not_72_out, opd[3]);
  not not_73 (not_73_out, opd[0]);
  not not_74 (not_74_out, opm[4]);
  not not_75 (not_75_out, opm[3]);
  not not_76 (not_76_out, opm[2]);
  not not_77 (not_77_out, opm[1]);
  not not_78 (not_78_out, opm[0]);
  not not_79 (not_79_out, opm[4]);
  not not_80 (not_80_out, opm[2]);
  not not_81 (not_81_out, opm[1]);
  not not_82 (not_82_out, opm[0]);
  not not_83 (not_83_out, opm[4]);
  not not_84 (not_84_out, opm[3]);
  not not_85 (not_85_out, opm[1]);
  not not_86 (not_86_out, opm[3]);
  not not_87 (not_87_out, opm[1]);
  not not_88 (not_88_out, opm[4]);
  not not_89 (not_89_out, opm[3]);
  not not_90 (not_90_out, opm[2]);
  not not_91 (not_91_out, opd[4]);
  not not_92 (not_92_out, opd[3]);
  not not_93 (not_93_out, opd[1]);
  not not_94 (not_94_out, opd[0]);
  and and_23 (bne_2, not_67_out, not_68_out, not_69_out, opd[1], not_70_out);
  and and_24 (blt, not_71_out, not_72_out, opd[2], opd[1], not_73_out);
  and and_25 (and_25_out, not_74_out, not_75_out, not_76_out, not_77_out, not_78_out);
  and and_26 (and_26_out, not_79_out, opm[3], not_80_out, not_81_out, not_82_out);
  and and_27 (and_27_out, not_83_out, not_84_out, opm[2], not_85_out, opm[0]);
  and and_28 (and_28_out, opm[4], not_86_out, opm[2], not_87_out, opm[0]);
  and and_29 (and_29_out, not_88_out, not_89_out, not_90_out, opm[1], opm[0]);
  and and_30 (and_30_out, not_91_out, not_92_out, opd[2], not_93_out, not_94_out);
  Comparator #(.width(5)) comparator_1 (.a(rdm), .b(rdd), .eq(comparator_1_eq));  // open: gt, lt
  or or_5 (or_5_out, and_25_out, and_26_out, and_27_out, and_28_out, and_29_out);
  not not_95 (not_95_out, comparator_2_eq);
  Comparator #(.width(5)) comparator_2 (.a({5{1'b0}}), .b(rdm), .eq(comparator_2_eq));  // open: gt, lt
  Comparator #(.width(5)) comparator_3 (.a(rdd), .b({5{1'b0}}), .eq(comparator_3_eq));  // open: gt, lt
  and and_31 (jrbyp, or_5_out, and_30_out, not_95_out, comparator_1_eq, not_96_out);
  not not_96 (not_96_out, comparator_3_eq);

  assign XC2 = XC1;
endmodule

module Hazard (
  input  [4:0] FDRS1,
  input  [4:0] DXRD,
  input  [4:0] XMRD,
  input  [4:0] FDRS2,
  input  [31:0] IRM,
  input  [31:0] IRW,
  input  [4:0] Dop,
  output out_8
);

  wire and_1_out, and_2_out, and_3_out, comparator_1_eq, comparator_2_eq, comparator_3_eq, comparator_4_eq,
       comparator_5_eq, comparator_6_eq, comparator_7_eq, comparator_8_eq, comparator_9_eq, comparator_10_eq,
       not_1_out, not_2_out, not_3_out, not_4_out, or_1_out, or_2_out, or_3_out, or_4_out;

  Comparator #(.width(32)) comparator_1 (.a(IRM), .b({32{1'b0}}), .eq(comparator_1_eq));  // open: gt, lt
  Comparator #(.width(32)) comparator_2 (.a(IRW), .b({32{1'b0}}), .eq(comparator_2_eq));  // open: gt, lt
  Comparator #(.width(5)) comparator_3 (.a(Dop), .b(5'b00011), .eq(comparator_3_eq));  // open: gt, lt
  Comparator #(.width(5)) comparator_4 (.a(Dop), .b(5'b10101), .eq(comparator_4_eq));  // open: gt, lt
  Comparator #(.width(5)) comparator_5 (.a(FDRS1), .b(DXRD), .eq(comparator_5_eq));  // open: gt, lt
  Comparator #(.width(5)) comparator_6 (.a(FDRS1), .b(XMRD), .eq(comparator_6_eq));  // open: gt, lt
  Comparator #(.width(5)) comparator_7 (.a(FDRS2), .b(DXRD), .eq(comparator_7_eq));  // open: gt, lt
  Comparator #(.width(5)) comparator_8 (.a(FDRS2), .b(XMRD), .eq(comparator_8_eq));  // open: gt, lt
  not not_1 (not_1_out, comparator_1_eq);
  not not_2 (not_2_out, comparator_2_eq);
  or or_1 (or_1_out, comparator_3_eq, comparator_4_eq);
  or or_2 (or_2_out, comparator_5_eq, comparator_7_eq);
  or or_3 (or_3_out, comparator_6_eq, comparator_8_eq);
  or or_4 (or_4_out, not_1_out, not_2_out);
  and and_1 (and_1_out, or_4_out, or_1_out);
  Comparator #(.width(5)) comparator_9 (.a(DXRD), .b({5{1'b0}}), .eq(comparator_9_eq));  // open: gt, lt
  Comparator #(.width(5)) comparator_10 (.a(XMRD), .b({5{1'b0}}), .eq(comparator_10_eq));  // open: gt, lt
  not not_3 (not_3_out, comparator_9_eq);
  not not_4 (not_4_out, comparator_10_eq);
  and and_2 (and_2_out, not_3_out, or_2_out);
  or or_5 (out_8, and_2_out, and_1_out, and_3_out);
  and and_3 (and_3_out, or_3_out, not_4_out);
endmodule

module Stall (
  input  [4:0] DXOp,
  input  [4:0] FDRS1,
  input  [4:0] FDRS2,
  input  [4:0] DXRD,
  input  [4:0] FDOp,
  input  [4:0] FOp,
  output stall,
  output PC_nonen
);

  wire and_2_out, and_3_out, comparator_1_eq, comparator_2_eq, comparator_3_eq, comparator_4_eq,
       comparator_6_eq, comparator_7_eq, comparator_8_eq, comparator_9_eq, comparator_10_eq,
       comparator_11_eq, not_1_out, or_1_out, or_2_out;
  wire [4:0] not_2_out;

  Comparator #(.width(5)) comparator_1 (.a(DXRD), .b({5{1'b0}}), .eq(comparator_1_eq));  // open: gt, lt
  not not_1 (not_1_out, comparator_1_eq);
  assign not_2_out = ~5'b11100;  // NOT_Gate not_2, 5 bits wide
  Comparator #(.width(5)) comparator_2 (.a(FDOp), .b(5'b00001), .eq(comparator_2_eq));  // open: gt, lt
  Comparator #(.width(5)) comparator_3 (.a(FDOp), .b(5'b00011), .eq(comparator_3_eq));  // open: gt, lt
  Comparator #(.width(5)) comparator_4 (.a(FDOp), .b(5'b00100), .eq(comparator_4_eq));  // open: gt, lt
  Comparator #(.width(5)) comparator_5 (.a(FDOp), .b(5'b10110), .eq(comparator_4_eq));  // open: gt, lt
  Comparator #(.width(5)) comparator_6 (.a(FOp), .b(5'b00010), .eq(comparator_6_eq));  // open: gt, lt
  Comparator #(.width(5)) comparator_7 (.a(FOp), .b(5'b00110), .eq(comparator_7_eq));  // open: gt, lt
  Comparator #(.width(5)) comparator_8 (.a(DXOp), .b(5'b00010), .eq(comparator_8_eq));  // open: gt, lt
  Comparator #(.width(5)) comparator_9 (.a(FDRS1), .b(DXRD), .eq(comparator_9_eq));  // open: gt, lt
  Comparator #(.width(5)) comparator_10 (.a(FDRS2), .b(DXRD), .eq(comparator_10_eq));  // open: gt, lt
  Comparator #(.width(5)) comparator_11 (.a(not_2_out), .b(FDOp), .eq(comparator_11_eq));  // open: gt, lt
  or or_1 (or_1_out, comparator_2_eq, comparator_3_eq, comparator_4_eq, comparator_4_eq);
  or or_2 (or_2_out, comparator_6_eq, comparator_7_eq);
  and and_1 (PC_nonen, or_1_out, or_2_out);
  and and_2 (and_2_out, not_1_out, comparator_8_eq, comparator_9_eq);
  and and_3 (and_3_out, not_1_out, comparator_10_eq, comparator_11_eq);
  or or_3 (stall, and_2_out, and_3_out);
endmodule

module Bypass (
  input  [4:0] DXRS1,
  input  [4:0] XMRD,
  input  [4:0] Xop,
  input  [4:0] MWRD,
  input  [4:0] Mop,
  input  [4:0] DRD,
  input  [4:0] MRD,
  input  [4:0] XRD,
  input  [4:0] DXRS2,
  input  [4:0] WOp,
  output Mbyp1,
  output Wbyp,
  output swbyp,
  output Mbyp2,
  output Wbyp2,
  output bypout
);

  wire and_1_out, and_2_out, and_3_out, and_4_out, and_5_out, and_6_out, and_7_out, and_8_out, and_9_out,
       and_11_out, and_12_out, and_13_out, and_14_out, and_15_out, and_16_out, and_17_out, and_18_out,
       and_19_out, and_20_out, and_21_out, and_22_out, and_23_out, and_24_out, and_25_out, and_26_out,
       and_27_out, and_28_out, and_30_out, and_31_out, comparator_1_eq, comparator_2_eq, comparator_3_eq,
       comparator_4_eq, comparator_5_eq, comparator_6_eq, comparator_7_eq, comparator_8_eq, comparator_9_eq,
       comparator_10_eq, comparator_11_eq, comparator_12_eq, comparator_13_eq, comparator_14_eq,
       comparator_15_eq, comparator_16_eq, comparator_17_eq, comparator_18_eq, comparator_19_eq,
       comparator_20_eq, comparator_21_eq, comparator_22_eq, comparator_23_eq, comparator_24_eq,
       comparator_25_eq, comparator_26_eq, comparator_27_eq, comparator_28_eq, comparator_29_eq, not_1_out,
       not_2_out, not_3_out, not_4_out, not_5_out, not_6_out, not_7_out, not_8_out, not_9_out, not_10_out,
       not_11_out, not_12_out, not_13_out, not_14_out, not_15_out, not_16_out, not_17_out, not_18_out,
       not_19_out, not_20_out, not_21_out, not_22_out, not_23_out, not_24_out, not_25_out, not_26_out,
       not_27_out, not_28_out, not_29_out, or_1_out;

  Comparator #(.width(5)) comparator_1 (.a(DXRS1), .b(XMRD), .eq(comparator_1_eq));  // open: gt, lt
  Comparator #(.width(5)) comparator_2 (.a(DXRS1), .b(MWRD), .eq(comparator_2_eq));  // open: gt, lt
  Comparator #(.width(5)) comparator_3 (.a(DXRS2), .b(XMRD), .eq(comparator_3_eq));  // open: gt, lt
  Comparator #(.width(5)) comparator_4 (.a(DXRS2), .b(MWRD), .eq(comparator_4_eq));  // open: gt, lt
  Comparator #(.width(5)) comparator_5 (.a(WOp), .b({5{1'b0}}), .eq(comparator_5_eq));  // open: gt, lt
  Comparator #(.width(5)) comparator_6 (.a(WOp), .b(5'b00101), .eq(comparator_6_eq));  // open: gt, lt
  Comparator #(.width(5)) comparator_7 (.a(MWRD), .b({5{1'b0}}), .eq(comparator_7_eq));  // open: gt, lt
  Comparator #(.width(5)) comparator_8 (.a(XMRD), .b({5{1'b0}}), .eq(comparator_8_eq));  // open: gt, lt
  Comparator #(.width(5)) comparator_9 (.a({5{1'b0}}), .b(DXRS1), .eq(comparator_9_eq));  // open: gt, lt
  and and_1 (and_1_out, comparator_9_eq, comparator_10_eq);
  Comparator #(.width(5)) comparator_10 (.a({5{1'b0}}), .b(XMRD), .eq(comparator_10_eq));  // open: gt, lt
  Comparator #(.width(5)) comparator_11 (.a(MWRD), .b({5{1'b0}}), .eq(comparator_11_eq));  // open: gt, lt
  Comparator #(.width(5)) comparator_12 (.a(DXRS1), .b({5{1'b0}}), .eq(comparator_12_eq));  // open: gt, lt
  Comparator #(.width(5)) comparator_13 (.a({5{1'b0}}), .b(DXRS2), .eq(comparator_13_eq));  // open: gt, lt
  and and_2 (and_2_out, comparator_13_eq, comparator_14_eq);
  Comparator #(.width(5)) comparator_14 (.a({5{1'b0}}), .b(XMRD), .eq(comparator_14_eq));  // open: gt, lt
  Comparator #(.width(5)) comparator_15 (.a(MWRD), .b({5{1'b0}}), .eq(comparator_15_eq));  // open: gt, lt
  Comparator #(.width(5)) comparator_16 (.a(DXRS2), .b({5{1'b0}}), .eq(comparator_16_eq));  // open: gt, lt
  Comparator #(.width(5)) comparator_17 (.a(XMRD), .b(MWRD), .eq(comparator_17_eq));  // open: gt, lt
  not not_1 (not_1_out, and_1_out);
  and and_3 (and_3_out, not_1_out, comparator_1_eq);
  not not_2 (not_2_out, and_4_out);
  and and_4 (and_4_out, comparator_11_eq, comparator_12_eq);
  not not_3 (not_3_out, and_2_out);
  and and_5 (and_5_out, not_3_out, comparator_3_eq);
  not not_4 (not_4_out, and_6_out);
  and and_6 (and_6_out, comparator_15_eq, comparator_16_eq);
  Comparator #(.width(5)) comparator_18 (.a(WOp), .b(5'b00111), .eq(comparator_18_eq));  // open: gt, lt
  Comparator #(.width(5)) comparator_19 (.a(WOp), .b(5'b01000), .eq(comparator_19_eq));  // open: gt, lt
  and and_7 (and_7_out, comparator_7_eq, comparator_8_eq);
  and and_8 (and_8_out, comparator_2_eq, not_2_out);
  and and_9 (and_9_out, comparator_4_eq, not_4_out);
  or or_1 (or_1_out, comparator_18_eq, comparator_5_eq, comparator_6_eq, comparator_19_eq);
  and and_10 (bypout, or_1_out, comparator_17_eq, not_5_out);
  not not_5 (not_5_out, and_7_out);
  or or_2 (Mbyp1, and_3_out, and_27_out);
  or or_3 (Wbyp, and_8_out, and_11_out);
  and and_11 (and_11_out, and_27_out, and_14_out);
  or or_4 (Mbyp2, and_5_out, and_21_out, swbyp, and_26_out);
  or or_5 (Wbyp2, and_9_out, and_21_out, and_12_out);
  and and_12 (and_12_out, and_26_out, and_14_out);
  not not_6 (not_6_out, Xop[4]);
  not not_7 (not_7_out, Xop[3]);
  not not_8 (not_8_out, Xop[0]);
  not not_9 (not_9_out, Mop[4]);
  not not_10 (not_10_out, Mop[2]);
  not not_11 (not_11_out, Mop[1]);
  not not_12 (not_12_out, Mop[0]);
  Comparator #(.width(5)) comparator_20 (.a(DRD), .b(MRD), .eq(comparator_20_eq));  // open: gt, lt
  not not_13 (not_13_out, Xop[3]);
  not not_14 (not_14_out, Xop[0]);
  not not_15 (not_15_out, Mop[4]);
  not not_16 (not_16_out, Mop[2]);
  not not_17 (not_17_out, Mop[1]);
  not not_18 (not_18_out, Mop[0]);
  Comparator #(.width(5)) comparator_21 (.a(DXRS1), .b(MRD), .eq(comparator_21_eq));  // open: gt, lt
  and and_13 (and_13_out, not_6_out, not_7_out, Xop[1], not_8_out);
  and and_14 (and_14_out, not_9_out, Mop[3], not_10_out, not_11_out, not_12_out);
  Comparator #(.width(5)) comparator_22 (.a(MRD), .b({5{1'b0}}), .eq(comparator_22_eq));  // open: gt, lt
  Comparator #(.width(5)) comparator_23 (.a(DRD), .b({5{1'b0}}), .eq(comparator_23_eq));  // open: gt, lt
  and and_15 (and_15_out, Xop[4], not_13_out, Xop[2], Xop[1], not_14_out);
  and and_16 (and_16_out, not_15_out, Mop[3], not_16_out, not_17_out, not_18_out);
  Comparator #(.width(5)) comparator_24 (.a(5'b11110), .b(MRD), .eq(comparator_24_eq));  // open: gt, lt
  not not_19 (not_19_out, Xop[3]);
  and and_17 (and_17_out, not_19_out, Xop[1], not_20_out);
  not not_20 (not_20_out, Xop[0]);
  not not_21 (not_21_out, Mop[4]);
  not not_22 (not_22_out, Mop[2]);
  and and_18 (and_18_out, not_21_out, Mop[3], not_22_out, not_23_out, not_24_out);
  not not_23 (not_23_out, Mop[1]);
  not not_24 (not_24_out, Mop[0]);
  Comparator #(.width(5)) comparator_25 (.a(MRD), .b({5{1'b0}}), .eq(comparator_25_eq));  // open: gt, lt
  Comparator #(.width(5)) comparator_26 (.a(DXRS1), .b({5{1'b0}}), .eq(comparator_26_eq));  // open: gt, lt
  buf and_19 (and_19_out, and_13_out);  // AND_Gate
  not not_25 (not_25_out, and_20_out);
  and and_20 (and_20_out, comparator_22_eq, comparator_23_eq);
  and and_21 (and_21_out, and_15_out, and_16_out, comparator_24_eq);
  and and_22 (and_22_out, and_17_out, and_18_out);
  not not_26 (not_26_out, and_23_out);
  and and_23 (and_23_out, comparator_25_eq, comparator_26_eq);
  and and_24 (and_24_out, comparator_20_eq, not_25_out);
  and and_25 (and_25_out, comparator_21_eq, not_26_out);
  and and_26 (and_26_out, and_19_out, and_24_out);
  and and_27 (and_27_out, and_22_out, and_25_out);
  not not_27 (not_27_out, Xop[4]);
  not not_28 (not_28_out, Xop[3]);
  and and_28 (and_28_out, not_27_out, not_28_out, Xop[2], Xop[1], Xop[0]);
  and and_29 (swbyp, and_28_out, and_31_out);
  Comparator #(.width(5)) comparator_27 (.a(MWRD), .b(XRD), .eq(comparator_27_eq));  // open: gt, lt
  Comparator #(.width(5)) comparator_28 (.a(XRD), .b({5{1'b0}}), .eq(comparator_28_eq));  // open: gt, lt
  Comparator #(.width(5)) comparator_29 (.a(MWRD), .b({5{1'b0}}), .eq(comparator_29_eq));  // open: gt, lt
  and and_30 (and_30_out, comparator_28_eq, comparator_29_eq);
  not not_29 (not_29_out, and_30_out);
  and and_31 (and_31_out, comparator_27_eq, not_29_out);

  // Notes on the sheet:
  //   Disconnected to see if ALU Operations bypass proprly in branch ops
endmodule

module RStatus (
  input  [4:0] ALUOp,
  input  ovf,
  input  [4:0] OP,
  input  [31:0] Target,
  output statuswrite,
  output [31:0] writeout
);

  wire and_1_out, and_2_out, and_3_out, and_4_out, and_5_out, and_6_out, not_1_out, not_2_out, not_3_out,
       not_4_out, not_5_out, not_6_out, not_7_out, not_8_out, not_9_out, not_10_out, not_11_out, not_12_out,
       not_13_out, not_14_out, not_15_out, not_16_out, not_17_out, not_18_out, not_19_out, or_1_out, or_2_out;
  wire [1:0] or_3_out;

  not not_1 (not_1_out, OP[4]);
  not not_2 (not_2_out, OP[3]);
  and and_1 (and_1_out, not_1_out, not_2_out, not_3_out, not_4_out, not_5_out);
  not not_3 (not_3_out, OP[2]);
  not not_4 (not_4_out, OP[1]);
  not not_5 (not_5_out, OP[0]);
  not not_6 (not_6_out, OP[4]);
  not not_7 (not_7_out, OP[3]);
  and and_2 (and_2_out, not_6_out, not_7_out, OP[2], not_8_out, OP[0]);
  not not_8 (not_8_out, OP[1]);
  not not_9 (not_9_out, OP[3]);
  and and_3 (and_3_out, OP[4], not_9_out, OP[2], not_10_out, OP[0]);
  not not_10 (not_10_out, OP[1]);
  Multiplexer #(.select(2), .width(32), .enable("false")) multiplexer_1 (
    .in0(32'h1), .in1(32'h2), .in2(32'h3), .in3(Target), .out(writeout), .sel(or_3_out));
  not not_11 (not_11_out, ALUOp[4]);
  not not_12 (not_12_out, ALUOp[3]);
  not not_13 (not_13_out, ALUOp[2]);
  and and_4 (and_4_out, not_11_out, not_12_out, not_13_out, not_14_out, not_15_out);
  not not_14 (not_14_out, ALUOp[1]);
  not not_15 (not_15_out, ALUOp[0]);
  not not_16 (not_16_out, ALUOp[4]);
  not not_17 (not_17_out, ALUOp[3]);
  and and_5 (and_5_out, not_16_out, not_17_out, not_18_out, not_19_out, ALUOp[0]);
  not not_18 (not_18_out, ALUOp[2]);
  not not_19 (not_19_out, ALUOp[1]);
  or or_1 (or_1_out, and_6_out, and_2_out, and_3_out);
  or or_2 (or_2_out, and_4_out, and_5_out);
  and and_6 (and_6_out, or_2_out, and_1_out);
  or or_3 (or_3_out[0], and_2_out, and_3_out);
  or or_4 (or_3_out[1], and_5_out, and_3_out);
  and and_7 (statuswrite, or_1_out, ovf);
endmodule

// predict
module brch_predictor (
  input  [31:0] brch_update_pc,
  input  reset,
  input  clk,
  input  brch_update,
  input  brch_taken,
  input  [31:0] pc1,
  input  [31:0] isn,
  input  [31:0] brch_update_inst,
  output brch_pred,
  output [31:0] pc_no_pred,
  output [31:0] pc_pred,
  output if_brch_inst
);

  wire and_1_out, and_2_out, and_3_out, and_4_out, and_5_out, and_6_out, and_7_out, and_8_out, and_9_out,
       and_10_out, and_11_out, and_12_out, and_13_out, and_14_out, and_15_out, and_16_out, and_17_out,
       and_18_out, and_19_out, and_20_out, and_21_out, and_22_out, and_23_out, and_24_out, and_25_out,
       and_26_out, and_27_out, and_28_out, and_29_out, and_30_out, and_31_out, and_32_out, and_33_out,
       and_34_out, and_35_out, and_36_out, and_37_out, and_38_out, and_39_out, and_40_out, and_41_out,
       and_42_out, and_43_out, and_44_out, and_45_out, and_46_out, comparator_1_eq, comparator_2_eq,
       comparator_3_eq, comparator_4_eq, comparator_5_eq, comparator_6_eq, comparator_7_eq, comparator_8_eq,
       comparator_9_eq, comparator_10_eq, comparator_11_eq, comparator_12_eq, comparator_13_eq,
       comparator_14_eq, comparator_15_eq, comparator_16_eq, comparator_17_eq, comparator_18_eq,
       comparator_19_eq, comparator_20_eq, comparator_21_eq, comparator_22_eq, comparator_23_eq,
       comparator_24_eq, comparator_25_eq, comparator_26_eq, comparator_27_eq, comparator_28_eq,
       comparator_29_eq, controlled_buffer_1_out, controlled_buffer_2_out, controlled_buffer_3_out,
       controlled_buffer_4_out, controlled_buffer_5_out, controlled_buffer_6_out, controlled_buffer_7_out,
       controlled_buffer_8_out, controlled_buffer_9_out, d_ff_1_q, d_ff_2_q, d_ff_3_q, d_ff_4_q, d_ff_5_q,
       d_ff_6_q, d_ff_7_q, d_ff_8_q, d_ff_9_q, d_ff_10_q, d_ff_11_q, d_ff_12_q, d_ff_13_q, d_ff_14_q,
       d_ff_15_q, d_ff_16_q, d_ff_17_q, d_ff_18_q, demultiplexer_1_out0, demultiplexer_1_out1,
       demultiplexer_2_out0, demultiplexer_2_out1, demultiplexer_3_out0, demultiplexer_3_out1,
       demultiplexer_4_out0, demultiplexer_4_out1, demultiplexer_5_out0, demultiplexer_5_out1,
       demultiplexer_6_out0, demultiplexer_6_out1, demultiplexer_7_out0, demultiplexer_7_out1,
       demultiplexer_8_out0, demultiplexer_8_out1, demultiplexer_9_out0, demultiplexer_9_out1,
       demultiplexer_10_out0, demultiplexer_10_out1, demultiplexer_11_out0, demultiplexer_11_out1,
       demultiplexer_12_out0, demultiplexer_12_out1, demultiplexer_13_out0, demultiplexer_13_out1,
       demultiplexer_14_out0, demultiplexer_14_out1, demultiplexer_15_out0, demultiplexer_15_out1,
       demultiplexer_16_out0, demultiplexer_16_out1, demultiplexer_17_out0, demultiplexer_17_out1,
       demultiplexer_18_out0, demultiplexer_18_out1, demultiplexer_19_out0, demultiplexer_19_out1,
       demultiplexer_20_out0, demultiplexer_20_out1, demultiplexer_21_out0, demultiplexer_21_out1,
       n32_bit_compact_2_ovf, not_1_out, not_2_out, not_3_out, not_4_out, not_5_out, not_6_out, not_7_out,
       not_8_out, not_9_out, not_10_out, not_11_out, not_12_out, not_13_out, not_14_out, not_15_out,
       not_16_out, not_17_out, not_18_out, not_19_out, not_20_out, not_21_out, not_22_out, not_23_out,
       not_24_out, not_25_out, not_26_out, not_27_out, not_28_out, not_29_out, not_30_out, not_31_out,
       not_32_out, not_33_out, not_34_out, not_35_out, not_36_out, not_37_out, not_38_out, not_39_out,
       not_40_out, not_41_out, not_42_out, not_43_out, not_44_out, not_45_out, not_46_out, not_47_out,
       not_48_out, or_1_out, or_3_out, or_4_out, or_5_out, or_6_out, or_7_out, or_8_out, or_9_out, or_10_out,
       or_11_out, or_13_out;
  wire [2:0] bit_extender_2_out;
  wire [5:0] bit_extender_3_out, bit_extender_4_out, bit_extender_5_out, bit_extender_6_out,
       bit_extender_7_out, bit_extender_8_out, bit_extender_9_out, bit_extender_10_out, bit_extender_11_out,
       bit_extender_12_out, bit_extender_13_out;
  wire [31:0] bit_extender_1_out, n32_bit_compact_1_result, n32_bit_compact_2_result, register_32_1_output,
       register_32_2_output, register_32_3_output, register_32_4_output, register_32_5_output,
       register_32_6_output, register_32_7_output, register_32_8_output, register_32_9_output;

  Demultiplexer #(.enable("false")) demultiplexer_1 (
    .out0(demultiplexer_1_out0), .out1(demultiplexer_1_out1), .in(demultiplexer_2_out0),
    .sel(bit_extender_2_out[1]));
  Demultiplexer #(.enable("false")) demultiplexer_2 (
    .out0(demultiplexer_2_out0), .out1(demultiplexer_2_out1), .in(and_1_out), .sel(bit_extender_2_out[2]));
  Demultiplexer #(.enable("false")) demultiplexer_3 (
    .out0(demultiplexer_3_out0), .out1(demultiplexer_3_out1), .in(demultiplexer_2_out1),
    .sel(bit_extender_2_out[1]));
  Demultiplexer #(.enable("false")) demultiplexer_4 (
    .out0(demultiplexer_4_out0), .out1(demultiplexer_4_out1), .in(demultiplexer_1_out0),
    .sel(bit_extender_2_out[0]));
  Demultiplexer #(.enable("false")) demultiplexer_5 (
    .out0(demultiplexer_5_out0), .out1(demultiplexer_5_out1), .in(demultiplexer_1_out1),
    .sel(bit_extender_2_out[0]));
  Demultiplexer #(.enable("false")) demultiplexer_6 (
    .out0(demultiplexer_6_out0), .out1(demultiplexer_6_out1), .in(demultiplexer_3_out0),
    .sel(bit_extender_2_out[0]));
  Demultiplexer #(.enable("false")) demultiplexer_7 (
    .out0(demultiplexer_7_out0), .out1(demultiplexer_7_out1), .in(demultiplexer_3_out1),
    .sel(bit_extender_2_out[0]));
  and and_1 (and_1_out, clk, and_7_out);
  not not_1 (not_1_out, clk);
  and and_2 (and_2_out, d_ff_1_q, d_ff_2_q, not_2_out);
  not not_2 (not_2_out, brch_taken);
  not not_3 (not_3_out, d_ff_2_q);
  and and_3 (and_3_out, not_3_out, brch_taken, d_ff_1_q);
  and and_4 (and_4_out, d_ff_1_q, d_ff_2_q, brch_taken);
  and and_5 (and_5_out, brch_taken, not_4_out, d_ff_2_q);
  not not_4 (not_4_out, d_ff_1_q);
  assign bit_extender_1_out = {{15{1'b0}}, isn[16:0]};  // Bit_Extender bit_extender_1
  D_Flip_Flop d_ff_1 (.clk(brch_update), .D(brch_taken), .Q(d_ff_1_q));  // open: Qn, preset, en, reset
  D_Flip_Flop d_ff_2 (.clk(brch_update), .D(or_1_out), .Q(d_ff_2_q));  // open: Qn, preset, en, reset
  or or_1 (or_1_out, and_2_out, and_3_out, and_4_out, and_5_out);
  Comparator #(.width(5)) comparator_1 (.a(isn[31:27]), .b(5'b00010), .eq(comparator_1_eq));  // open: gt, lt
  Comparator #(.width(5)) comparator_2 (.a(isn[31:27]), .b(5'b00110), .eq(comparator_2_eq));  // open: gt, lt
  register_32 register_32_1 (
    .clk(not_1_out), .\input (n32_bit_compact_2_result), .enable(and_1_out), .\output (register_32_1_output),
    .reset(reset));
  Bit_Extender #(.in_width(32), .out_width(3)) bit_extender_2 (.in(register_32_1_output), .out(bit_extender_2_out));
  _32_bit_compact u_32_bit_compact_1 (
    .result(n32_bit_compact_1_result), .A(pc1), .B(bit_extender_1_out), .sub(1'b0));  // open: ovf
  or or_2 (if_brch_inst, comparator_1_eq, comparator_2_eq);
  register_32 register_32_2 (
    .clk(not_5_out), .\input (brch_update_pc), .enable(demultiplexer_4_out0),
    .\output (register_32_2_output), .reset(reset));
  register_32 register_32_3 (
    .clk(not_5_out), .\input (brch_update_pc), .enable(demultiplexer_4_out1),
    .\output (register_32_3_output), .reset(reset));
  register_32 register_32_4 (
    .clk(not_5_out), .\input (brch_update_pc), .enable(demultiplexer_5_out0),
    .\output (register_32_4_output), .reset(reset));
  register_32 register_32_5 (
    .clk(not_5_out), .\input (brch_update_pc), .enable(demultiplexer_5_out1),
    .\output (register_32_5_output), .reset(reset));
  _32_bit_compact u_32_bit_compact_2 (
    .result(n32_bit_compact_2_result), .A(32'h1), .B(register_32_1_output), .ovf(n32_bit_compact_2_ovf),
    .sub(1'b0));
  and and_6 (and_6_out, if_brch_inst, or_13_out);
  not not_5 (not_5_out, clk);
  Bit_Extender #(.in_width(32), .out_width(6)) bit_extender_3 (.in(register_32_2_output), .out(bit_extender_3_out));
  Bit_Extender #(.in_width(32), .out_width(6)) bit_extender_4 (.in(register_32_3_output), .out(bit_extender_4_out));
  Bit_Extender #(.in_width(32), .out_width(6)) bit_extender_5 (.in(register_32_4_output), .out(bit_extender_5_out));
  Bit_Extender #(.in_width(32), .out_width(6)) bit_extender_6 (.in(register_32_5_output), .out(bit_extender_6_out));
  and and_7 (and_7_out, and_9_out, or_3_out);
  register_32 register_32_6 (
    .clk(not_5_out), .\input (brch_update_pc), .enable(demultiplexer_6_out0),
    .\output (register_32_6_output), .reset(reset));
  Bit_Extender #(.in_width(32), .out_width(6)) bit_extender_7 (.in(register_32_6_output), .out(bit_extender_7_out));
  Bit_Extender #(.in_width(32), .out_width(6)) bit_extender_8 (.in(register_32_7_output), .out(bit_extender_8_out));
  register_32 register_32_7 (
    .clk(not_5_out), .\input (brch_update_pc), .enable(demultiplexer_6_out1),
    .\output (register_32_7_output), .reset(reset));
  Bit_Extender #(.in_width(32), .out_width(6)) bit_extender_9 (.in(register_32_8_output), .out(bit_extender_9_out));
  register_32 register_32_8 (
    .clk(not_5_out), .\input (brch_update_pc), .enable(demultiplexer_7_out0),
    .\output (register_32_8_output), .reset(reset));
  Bit_Extender #(.in_width(32), .out_width(6)) bit_extender_10 (.in(register_32_9_output), .out(bit_extender_10_out));
  register_32 register_32_9 (
    .clk(not_5_out), .\input (brch_update_pc), .enable(demultiplexer_7_out1),
    .\output (register_32_9_output), .reset(reset));
  Multiplexer #(.width(32), .enable("false")) multiplexer_1 (
    .in0(pc1), .in1(n32_bit_compact_1_result), .out(pc_pred), .sel(and_6_out));
  Bit_Extender #(.in_width(32), .out_width(6)) bit_extender_11 (.in(pc1), .out(bit_extender_11_out));
  Comparator #(.width(5)) comparator_3 (
    .a(brch_update_inst[31:27]), .b(5'b00010), .eq(comparator_3_eq));  // open: gt, lt
  Comparator #(.width(5)) comparator_4 (
    .a(brch_update_inst[31:27]), .b(5'b00110), .eq(comparator_4_eq));  // open: gt, lt
  Bit_Extender #(.in_width(32), .out_width(6)) bit_extender_12 (.in(brch_update_pc), .out(bit_extender_12_out));
  or or_3 (or_3_out, comparator_3_eq, comparator_4_eq);
  Comparator #(.width(6)) comparator_5 (
    .a(bit_extender_12_out), .b(bit_extender_3_out), .eq(comparator_5_eq));  // open: gt, lt
  Comparator #(.width(6)) comparator_6 (
    .a(bit_extender_12_out), .b(bit_extender_4_out), .eq(comparator_6_eq));  // open: gt, lt
  Comparator #(.width(6)) comparator_7 (
    .a(bit_extender_12_out), .b(bit_extender_5_out), .eq(comparator_7_eq));  // open: gt, lt
  Comparator #(.width(6)) comparator_8 (
    .a(bit_extender_12_out), .b(bit_extender_6_out), .eq(comparator_8_eq));  // open: gt, lt
  Comparator #(.width(6)) comparator_9 (
    .a(bit_extender_12_out), .b(bit_extender_7_out), .eq(comparator_9_eq));  // open: gt, lt
  Comparator #(.width(6)) comparator_10 (
    .a(bit_extender_12_out), .b(bit_extender_8_out), .eq(comparator_10_eq));  // open: gt, lt
  Comparator #(.width(6)) comparator_11 (
    .a(bit_extender_12_out), .b(bit_extender_9_out), .eq(comparator_11_eq));  // open: gt, lt
  Comparator #(.width(6)) comparator_12 (
    .a(bit_extender_12_out), .b(bit_extender_10_out), .eq(comparator_12_eq));  // open: gt, lt
  assign controlled_buffer_1_out = comparator_12_eq ? not_6_out : 1'bz;  // Controlled_Buffer controlled_buffer_1
  not not_6 (not_6_out, and_8_out);
  and and_8 (and_8_out, brch_update, clk);
  not not_7 (not_7_out, comparator_12_eq);
  Bit_Extender #(.in_width(32), .out_width(6)) bit_extender_13 (.in(pc1), .out(bit_extender_13_out));
  assign controlled_buffer_2_out = comparator_11_eq ? not_6_out : 1'bz;  // Controlled_Buffer controlled_buffer_2
  assign controlled_buffer_3_out = comparator_10_eq ? not_6_out : 1'bz;  // Controlled_Buffer controlled_buffer_3
  assign controlled_buffer_4_out = comparator_9_eq ? not_6_out : 1'bz;  // Controlled_Buffer controlled_buffer_4
  assign controlled_buffer_5_out = comparator_8_eq ? not_6_out : 1'bz;  // Controlled_Buffer controlled_buffer_5
  not not_8 (not_8_out, comparator_9_eq);
  not not_9 (not_9_out, comparator_11_eq);
  not not_10 (not_10_out, comparator_10_eq);
  not not_11 (not_11_out, comparator_8_eq);
  and and_9 (and_9_out, not_7_out, not_9_out, not_10_out, not_8_out, not_11_out, not_15_out, not_14_out, not_13_out);
  not not_12 (not_12_out, brch_taken);
  Comparator #(.width(6)) comparator_13 (.a(bit_extender_3_out), .b({6{1'b0}}), .eq(comparator_13_eq));  // open: gt, lt
  Comparator #(.width(6)) comparator_14 (.a(bit_extender_4_out), .b({6{1'b0}}), .eq(comparator_14_eq));  // open: gt, lt
  Comparator #(.width(6)) comparator_15 (.a(bit_extender_5_out), .b({6{1'b0}}), .eq(comparator_15_eq));  // open: gt, lt
  Comparator #(.width(6)) comparator_16 (.a(bit_extender_6_out), .b({6{1'b0}}), .eq(comparator_16_eq));  // open: gt, lt
  Comparator #(.width(6)) comparator_17 (.a(bit_extender_7_out), .b({6{1'b0}}), .eq(comparator_17_eq));  // open: gt, lt
  Comparator #(.width(6)) comparator_18 (.a(bit_extender_8_out), .b({6{1'b0}}), .eq(comparator_18_eq));  // open: gt, lt
  Comparator #(.width(6)) comparator_19 (.a(bit_extender_9_out), .b({6{1'b0}}), .eq(comparator_19_eq));  // open: gt, lt
  Comparator #(.width(6)) comparator_20 (
    .a(bit_extender_10_out), .b({6{1'b0}}), .eq(comparator_20_eq));  // open: gt, lt
  Comparator #(.width(6)) comparator_21 (
    .a(bit_extender_13_out), .b({6{1'b0}}), .eq(comparator_21_eq));  // open: gt, lt
  assign controlled_buffer_6_out = comparator_7_eq ? not_6_out : 1'bz;  // Controlled_Buffer controlled_buffer_6
  assign controlled_buffer_7_out = comparator_6_eq ? not_6_out : 1'bz;  // Controlled_Buffer controlled_buffer_7
  assign controlled_buffer_8_out = comparator_5_eq ? not_6_out : 1'bz;  // Controlled_Buffer controlled_buffer_8
  not not_13 (not_13_out, comparator_5_eq);
  not not_14 (not_14_out, comparator_6_eq);
  not not_15 (not_15_out, comparator_7_eq);
  and and_10 (and_10_out, and_1_out, not_12_out);
  and and_11 (and_11_out, and_1_out, brch_taken);
  and and_12 (and_12_out, comparator_13_eq, comparator_14_eq, comparator_15_eq, comparator_16_eq, comparator_18_eq, comparator_19_eq, comparator_20_eq, comparator_17_eq);
  not not_16 (not_16_out, and_12_out);
  not not_17 (not_17_out, brch_taken);
  not not_18 (not_18_out, d_ff_4_q);
  not not_19 (not_19_out, d_ff_3_q);
  not not_20 (not_20_out, brch_taken);
  not not_21 (not_21_out, d_ff_6_q);
  not not_22 (not_22_out, d_ff_5_q);
  not not_23 (not_23_out, brch_taken);
  not not_24 (not_24_out, d_ff_8_q);
  not not_25 (not_25_out, d_ff_7_q);
  not not_26 (not_26_out, brch_taken);
  not not_27 (not_27_out, d_ff_10_q);
  not not_28 (not_28_out, d_ff_9_q);
  Demultiplexer #(.enable("false")) demultiplexer_8 (
    .out0(demultiplexer_8_out0), .out1(demultiplexer_8_out1), .in(and_10_out), .sel(bit_extender_2_out[2]));
  and and_13 (and_13_out, not_16_out, comparator_21_eq);
  and and_14 (and_14_out, d_ff_3_q, d_ff_4_q, not_17_out);
  and and_15 (and_15_out, not_18_out, brch_taken, d_ff_3_q);
  and and_16 (and_16_out, d_ff_3_q, d_ff_4_q, brch_taken);
  or or_4 (or_4_out, and_14_out, and_15_out, and_16_out, and_17_out);
  and and_17 (and_17_out, brch_taken, not_19_out, d_ff_4_q);
  and and_18 (and_18_out, d_ff_5_q, d_ff_6_q, not_20_out);
  and and_19 (and_19_out, not_21_out, brch_taken, d_ff_5_q);
  and and_20 (and_20_out, d_ff_5_q, d_ff_6_q, brch_taken);
  or or_5 (or_5_out, and_18_out, and_19_out, and_20_out, and_21_out);
  and and_21 (and_21_out, brch_taken, not_22_out, d_ff_6_q);
  and and_22 (and_22_out, d_ff_7_q, d_ff_8_q, not_23_out);
  and and_23 (and_23_out, not_24_out, brch_taken, d_ff_7_q);
  and and_24 (and_24_out, d_ff_7_q, d_ff_8_q, brch_taken);
  or or_6 (or_6_out, and_22_out, and_23_out, and_24_out, and_25_out);
  and and_25 (and_25_out, brch_taken, not_25_out, d_ff_8_q);
  and and_26 (and_26_out, d_ff_9_q, d_ff_10_q, not_26_out);
  and and_27 (and_27_out, not_27_out, brch_taken, d_ff_9_q);
  and and_28 (and_28_out, d_ff_9_q, d_ff_10_q, brch_taken);
  or or_7 (or_7_out, and_26_out, and_27_out, and_28_out, and_29_out);
  and and_29 (and_29_out, brch_taken, not_28_out, d_ff_10_q);
  Demultiplexer #(.enable("false")) demultiplexer_9 (
    .out0(demultiplexer_9_out0), .out1(demultiplexer_9_out1), .in(demultiplexer_11_out0),
    .sel(bit_extender_2_out[0]));
  Demultiplexer #(.enable("false")) demultiplexer_10 (
    .out0(demultiplexer_10_out0), .out1(demultiplexer_10_out1), .in(demultiplexer_11_out1),
    .sel(bit_extender_2_out[0]));
  Demultiplexer #(.enable("false")) demultiplexer_11 (
    .out0(demultiplexer_11_out0), .out1(demultiplexer_11_out1), .in(demultiplexer_8_out0),
    .sel(bit_extender_2_out[1]));
  Demultiplexer #(.enable("false")) demultiplexer_12 (
    .out0(demultiplexer_12_out0), .out1(demultiplexer_12_out1), .in(demultiplexer_13_out0),
    .sel(bit_extender_2_out[0]));
  Demultiplexer #(.enable("false")) demultiplexer_13 (
    .out0(demultiplexer_13_out0), .out1(demultiplexer_13_out1), .in(demultiplexer_8_out1),
    .sel(bit_extender_2_out[1]));
  Demultiplexer #(.enable("false")) demultiplexer_14 (
    .out0(demultiplexer_14_out0), .out1(demultiplexer_14_out1), .in(demultiplexer_13_out1),
    .sel(bit_extender_2_out[0]));
  D_Flip_Flop d_ff_3 (
    .clk(controlled_buffer_2_out), .D(brch_taken), .Q(d_ff_3_q), .preset(demultiplexer_21_out0),
    .reset(demultiplexer_14_out0));  // open: Qn, en
  D_Flip_Flop d_ff_4 (
    .clk(controlled_buffer_2_out), .D(or_4_out), .Q(d_ff_4_q), .preset(demultiplexer_21_out0),
    .reset(demultiplexer_14_out0));  // open: Qn, en
  D_Flip_Flop d_ff_5 (
    .clk(controlled_buffer_4_out), .D(brch_taken), .Q(d_ff_5_q), .preset(demultiplexer_20_out0),
    .reset(demultiplexer_12_out0));  // open: Qn, en
  D_Flip_Flop d_ff_6 (
    .clk(controlled_buffer_4_out), .D(or_5_out), .Q(d_ff_6_q), .preset(demultiplexer_20_out0),
    .reset(demultiplexer_12_out0));  // open: Qn, en
  D_Flip_Flop d_ff_7 (
    .clk(controlled_buffer_6_out), .D(brch_taken), .Q(d_ff_7_q), .preset(demultiplexer_19_out0),
    .reset(demultiplexer_10_out0));  // open: Qn, en
  D_Flip_Flop d_ff_8 (
    .clk(controlled_buffer_6_out), .D(or_6_out), .Q(d_ff_8_q), .preset(demultiplexer_19_out0),
    .reset(demultiplexer_10_out0));  // open: Qn, en
  D_Flip_Flop d_ff_9 (
    .clk(controlled_buffer_8_out), .D(brch_taken), .Q(d_ff_9_q), .preset(demultiplexer_18_out0),
    .reset(demultiplexer_9_out0));  // open: Qn, en
  D_Flip_Flop d_ff_10 (
    .clk(controlled_buffer_8_out), .D(or_7_out), .Q(d_ff_10_q), .preset(demultiplexer_18_out0),
    .reset(demultiplexer_9_out0));  // open: Qn, en
  and and_30 (and_30_out, d_ff_11_q, d_ff_12_q, not_29_out);
  not not_29 (not_29_out, brch_taken);
  not not_30 (not_30_out, d_ff_12_q);
  and and_31 (and_31_out, not_30_out, brch_taken, d_ff_11_q);
  and and_32 (and_32_out, d_ff_11_q, d_ff_12_q, brch_taken);
  not not_31 (not_31_out, d_ff_11_q);
  and and_33 (and_33_out, brch_taken, not_31_out, d_ff_12_q);
  and and_34 (and_34_out, d_ff_13_q, d_ff_14_q, not_32_out);
  not not_32 (not_32_out, brch_taken);
  not not_33 (not_33_out, d_ff_14_q);
  and and_35 (and_35_out, not_33_out, brch_taken, d_ff_13_q);
  and and_36 (and_36_out, d_ff_13_q, d_ff_14_q, brch_taken);
  and and_37 (and_37_out, brch_taken, not_34_out, d_ff_14_q);
  not not_34 (not_34_out, d_ff_13_q);
  and and_38 (and_38_out, d_ff_15_q, d_ff_16_q, not_35_out);
  not not_35 (not_35_out, brch_taken);
  not not_36 (not_36_out, d_ff_16_q);
  and and_39 (and_39_out, not_36_out, brch_taken, d_ff_15_q);
  and and_40 (and_40_out, d_ff_15_q, d_ff_16_q, brch_taken);
  not not_37 (not_37_out, d_ff_15_q);
  and and_41 (and_41_out, brch_taken, not_37_out, d_ff_16_q);
  and and_42 (and_42_out, d_ff_17_q, d_ff_18_q, not_38_out);
  not not_38 (not_38_out, brch_taken);
  not not_39 (not_39_out, d_ff_18_q);
  and and_43 (and_43_out, not_39_out, brch_taken, d_ff_17_q);
  and and_44 (and_44_out, d_ff_17_q, d_ff_18_q, brch_taken);
  and and_45 (and_45_out, brch_taken, not_40_out, d_ff_18_q);
  not not_40 (not_40_out, d_ff_17_q);
  Demultiplexer #(.enable("false")) demultiplexer_15 (
    .out0(demultiplexer_15_out0), .out1(demultiplexer_15_out1), .in(demultiplexer_16_out0),
    .sel(bit_extender_2_out[1]));
  Demultiplexer #(.enable("false")) demultiplexer_16 (
    .out0(demultiplexer_16_out0), .out1(demultiplexer_16_out1), .in(and_11_out), .sel(bit_extender_2_out[2]));
  Demultiplexer #(.enable("false")) demultiplexer_17 (
    .out0(demultiplexer_17_out0), .out1(demultiplexer_17_out1), .in(demultiplexer_16_out1),
    .sel(bit_extender_2_out[1]));
  D_Flip_Flop d_ff_11 (
    .clk(controlled_buffer_1_out), .D(brch_taken), .Q(d_ff_11_q), .preset(demultiplexer_21_out1),
    .reset(demultiplexer_14_out1));  // open: Qn, en
  D_Flip_Flop d_ff_12 (
    .clk(controlled_buffer_1_out), .D(or_8_out), .Q(d_ff_12_q), .preset(demultiplexer_21_out1),
    .reset(demultiplexer_14_out1));  // open: Qn, en
  or or_8 (or_8_out, and_30_out, and_31_out, and_32_out, and_33_out);
  D_Flip_Flop d_ff_13 (
    .clk(controlled_buffer_3_out), .D(brch_taken), .Q(d_ff_13_q), .preset(demultiplexer_20_out1),
    .reset(demultiplexer_12_out1));  // open: Qn, en
  D_Flip_Flop d_ff_14 (
    .clk(controlled_buffer_3_out), .D(or_9_out), .Q(d_ff_14_q), .preset(demultiplexer_20_out1),
    .reset(demultiplexer_12_out1));  // open: Qn, en
  or or_9 (or_9_out, and_34_out, and_35_out, and_36_out, and_37_out);
  D_Flip_Flop d_ff_15 (
    .clk(controlled_buffer_5_out), .D(brch_taken), .Q(d_ff_15_q), .preset(demultiplexer_19_out1),
    .reset(demultiplexer_10_out1));  // open: Qn, en
  D_Flip_Flop d_ff_16 (
    .clk(controlled_buffer_5_out), .D(or_10_out), .Q(d_ff_16_q), .preset(demultiplexer_19_out1),
    .reset(demultiplexer_10_out1));  // open: Qn, en
  or or_10 (or_10_out, and_38_out, and_39_out, and_40_out, and_41_out);
  D_Flip_Flop d_ff_17 (
    .clk(controlled_buffer_7_out), .D(brch_taken), .Q(d_ff_17_q), .preset(demultiplexer_18_out1),
    .reset(demultiplexer_9_out1));  // open: Qn, en
  D_Flip_Flop d_ff_18 (
    .clk(controlled_buffer_7_out), .D(or_11_out), .Q(d_ff_18_q), .preset(demultiplexer_18_out1),
    .reset(demultiplexer_9_out1));  // open: Qn, en
  or or_11 (or_11_out, and_42_out, and_43_out, and_44_out, and_45_out);
  Demultiplexer #(.enable("false")) demultiplexer_18 (
    .out0(demultiplexer_18_out0), .out1(demultiplexer_18_out1), .in(demultiplexer_15_out0),
    .sel(bit_extender_2_out[0]));
  Demultiplexer #(.enable("false")) demultiplexer_19 (
    .out0(demultiplexer_19_out0), .out1(demultiplexer_19_out1), .in(demultiplexer_15_out1),
    .sel(bit_extender_2_out[0]));
  Demultiplexer #(.enable("false")) demultiplexer_20 (
    .out0(demultiplexer_20_out0), .out1(demultiplexer_20_out1), .in(demultiplexer_17_out0),
    .sel(bit_extender_2_out[0]));
  Demultiplexer #(.enable("false")) demultiplexer_21 (
    .out0(demultiplexer_21_out0), .out1(demultiplexer_21_out1), .in(demultiplexer_17_out1),
    .sel(bit_extender_2_out[0]));
  assign controlled_buffer_9_out = comparator_29_eq ? d_ff_12_q : 1'bz;  // Controlled_Buffer controlled_buffer_9
  assign controlled_buffer_9_out = comparator_28_eq ? d_ff_4_q : 1'bz;  // Controlled_Buffer controlled_buffer_10
  not not_41 (not_41_out, comparator_27_eq);
  not not_42 (not_42_out, comparator_29_eq);
  not not_43 (not_43_out, comparator_28_eq);
  Comparator #(.width(6)) comparator_22 (
    .a(bit_extender_11_out), .b(bit_extender_3_out), .eq(comparator_22_eq));  // open: gt, lt
  Comparator #(.width(6)) comparator_23 (
    .a(bit_extender_11_out), .b(bit_extender_4_out), .eq(comparator_23_eq));  // open: gt, lt
  Comparator #(.width(6)) comparator_24 (
    .a(bit_extender_11_out), .b(bit_extender_5_out), .eq(comparator_24_eq));  // open: gt, lt
  Comparator #(.width(6)) comparator_25 (
    .a(bit_extender_11_out), .b(bit_extender_6_out), .eq(comparator_25_eq));  // open: gt, lt
  Comparator #(.width(6)) comparator_26 (
    .a(bit_extender_11_out), .b(bit_extender_7_out), .eq(comparator_26_eq));  // open: gt, lt
  Comparator #(.width(6)) comparator_27 (
    .a(bit_extender_11_out), .b(bit_extender_8_out), .eq(comparator_27_eq));  // open: gt, lt
  Comparator #(.width(6)) comparator_28 (
    .a(bit_extender_11_out), .b(bit_extender_9_out), .eq(comparator_28_eq));  // open: gt, lt
  Comparator #(.width(6)) comparator_29 (
    .a(bit_extender_11_out), .b(bit_extender_10_out), .eq(comparator_29_eq));  // open: gt, lt
  assign controlled_buffer_9_out = comparator_27_eq ? d_ff_14_q : 1'bz;  // Controlled_Buffer controlled_buffer_11
  assign controlled_buffer_9_out = comparator_26_eq ? d_ff_6_q : 1'bz;  // Controlled_Buffer controlled_buffer_12
  assign controlled_buffer_9_out = comparator_25_eq ? d_ff_16_q : 1'bz;  // Controlled_Buffer controlled_buffer_13
  assign controlled_buffer_9_out = comparator_24_eq ? d_ff_8_q : 1'bz;  // Controlled_Buffer controlled_buffer_14
  not not_44 (not_44_out, comparator_25_eq);
  not not_45 (not_45_out, comparator_23_eq);
  not not_46 (not_46_out, comparator_26_eq);
  not not_47 (not_47_out, comparator_24_eq);
  and and_46 (and_46_out, not_42_out, not_43_out, not_41_out, not_46_out, not_44_out, not_47_out, not_45_out, not_48_out);
  assign controlled_buffer_9_out = comparator_23_eq ? d_ff_18_q : 1'bz;  // Controlled_Buffer controlled_buffer_15
  assign controlled_buffer_9_out = comparator_22_eq ? d_ff_10_q : 1'bz;  // Controlled_Buffer controlled_buffer_16
  not not_48 (not_48_out, comparator_22_eq);
  or or_12 (brch_pred, or_13_out, and_13_out);
  or or_13 (or_13_out, and_46_out, controlled_buffer_9_out);

  assign pc_no_pred = pc1;
endmodule
module DB_byp (
  input  [4:0] Dop,
  input  [4:0] Mop,
  input  [4:0] Xop,
  input  [4:0] rdm,
  input  [4:0] rdx,
  input  [4:0] rdd,
  input  [4:0] rsd,
  output rdXbyp,
  output stall,
  output rsXbyp,
  output sextonbrchx,
  output rdMbyp,
  output rsMbyp,
  output rdMbyp2,
  output rsMbyp2,
  output sextonbrchm
);

  wire and_1_out, and_3_out, and_4_out, and_5_out, and_6_out, and_7_out, and_8_out, and_11_out, and_12_out,
       and_13_out, and_14_out, comparator_1_eq, comparator_2_eq, comparator_3_eq, comparator_4_eq,
       comparator_5_eq, comparator_6_eq, comparator_7_eq, comparator_8_eq, comparator_9_eq, comparator_10_eq,
       comparator_11_eq, comparator_12_eq, comparator_13_eq, comparator_14_eq, comparator_15_eq,
       comparator_16_eq, comparator_17_eq, comparator_18_eq, comparator_19_eq, comparator_20_eq,
       comparator_21_eq, comparator_22_eq, comparator_23_eq, comparator_24_eq, comparator_25_eq, not_1_out,
       not_2_out, not_3_out, not_4_out, or_1_out, or_2_out, or_3_out, or_7_out;

  Comparator #(.width(5)) comparator_1 (.a(Dop), .b(5'b00110), .eq(comparator_1_eq));  // open: gt, lt
  Comparator #(.width(5)) comparator_2 (.a(Dop), .b(5'b00100), .eq(comparator_2_eq));  // open: gt, lt
  Comparator #(.width(5)) comparator_3 (.a(Dop), .b(5'b00011), .eq(comparator_3_eq));  // open: gt, lt
  Comparator #(.width(5)) comparator_4 (.a(Dop), .b(5'b00010), .eq(comparator_4_eq));  // open: gt, lt
  Comparator #(.width(5)) comparator_5 (.a(Dop), .b(5'b00001), .eq(comparator_5_eq));  // open: gt, lt
  Comparator #(.width(5)) comparator_6 (.a(Xop), .b({5{1'b0}}), .eq(comparator_6_eq));  // open: gt, lt
  Comparator #(.width(5)) comparator_7 (.a(5'b01000), .b(Xop), .eq(comparator_7_eq));  // open: gt, lt
  Comparator #(.width(5)) comparator_8 (.a(5'b10101), .b(Xop), .eq(comparator_8_eq));  // open: gt, lt
  or or_1 (or_1_out, comparator_1_eq, comparator_2_eq, comparator_3_eq, comparator_4_eq, comparator_5_eq);
  and and_1 (and_1_out, or_1_out, comparator_6_eq);
  Comparator #(.width(5)) comparator_9 (.a(rdx), .b({5{1'b0}}), .eq(comparator_9_eq));  // open: gt, lt
  Comparator #(.width(5)) comparator_10 (.a(rdd), .b({5{1'b0}}), .eq(comparator_10_eq));  // open: gt, lt
  or or_2 (or_2_out, comparator_9_eq, comparator_10_eq);
  not not_1 (not_1_out, or_2_out);
  Comparator #(.width(5)) comparator_11 (.a(rdx), .b({5{1'b0}}), .eq(comparator_11_eq));  // open: gt, lt
  not not_2 (not_2_out, comparator_11_eq);
  Comparator #(.width(5)) comparator_12 (.a(rdd), .b(rdx), .eq(comparator_12_eq));  // open: gt, lt
  Comparator #(.width(5)) comparator_13 (.a(rdx), .b(rsd), .eq(comparator_13_eq));  // open: gt, lt
  Comparator #(.width(5)) comparator_14 (.a(Mop), .b({5{1'b0}}), .eq(comparator_14_eq));  // open: gt, lt
  Comparator #(.width(5)) comparator_15 (.a(5'b01000), .b(Mop), .eq(comparator_15_eq));  // open: gt, lt
  Comparator #(.width(5)) comparator_16 (.a(5'b10101), .b(Mop), .eq(comparator_16_eq));  // open: gt, lt
  and and_2 (stall, not_2_out, comparator_7_eq, or_1_out);
  and and_3 (and_3_out, and_1_out, comparator_12_eq);
  and and_4 (and_4_out, and_1_out, comparator_13_eq, not_1_out);
  Comparator #(.width(5)) comparator_17 (.a({5{1'b1}}), .b(rdd), .eq(comparator_17_eq));  // open: gt, lt
  Comparator #(.width(5)) comparator_18 (.a(rsd), .b({5{1'b1}}), .eq(comparator_18_eq));  // open: gt, lt
  and and_5 (and_5_out, or_1_out, comparator_14_eq);
  and and_6 (and_6_out, or_1_out, comparator_15_eq);
  not not_3 (not_3_out, comparator_19_eq);
  Comparator #(.width(5)) comparator_19 (.a(rdm), .b({5{1'b0}}), .eq(comparator_19_eq));  // open: gt, lt
  Comparator #(.width(5)) comparator_20 (.a({5{1'b1}}), .b(rsd), .eq(comparator_20_eq));  // open: gt, lt
  Comparator #(.width(5)) comparator_21 (.a(rdd), .b({5{1'b1}}), .eq(comparator_21_eq));  // open: gt, lt
  Comparator #(.width(5)) comparator_22 (.a(rdd), .b(rdm), .eq(comparator_22_eq));  // open: gt, lt
  Comparator #(.width(5)) comparator_23 (.a(rdm), .b(rsd), .eq(comparator_23_eq));  // open: gt, lt
  Comparator #(.width(5)) comparator_24 (.a(rdm), .b({5{1'b0}}), .eq(comparator_24_eq));  // open: gt, lt
  or or_3 (or_3_out, comparator_24_eq, comparator_25_eq);
  Comparator #(.width(5)) comparator_25 (.a(rsd), .b({5{1'b0}}), .eq(comparator_25_eq));  // open: gt, lt
  and and_7 (and_7_out, and_5_out, comparator_22_eq);
  and and_8 (and_8_out, and_5_out, comparator_23_eq);
  and and_9 (rdMbyp2, and_6_out, not_3_out, comparator_23_eq);
  and and_10 (rsMbyp2, and_6_out, not_3_out, comparator_22_eq);
  and and_11 (and_11_out, comparator_20_eq, comparator_16_eq);
  and and_12 (and_12_out, comparator_21_eq, comparator_16_eq);
  not not_4 (not_4_out, or_3_out);
  or or_4 (sextonbrchm, and_11_out, and_12_out);
  or or_5 (rdXbyp, and_13_out, and_3_out);
  or or_6 (rsXbyp, and_4_out, and_14_out);
  and and_13 (and_13_out, comparator_17_eq, comparator_8_eq);
  and and_14 (and_14_out, comparator_18_eq, comparator_8_eq);
  or or_7 (or_7_out, and_8_out, and_12_out);
  or or_8 (sextonbrchx, and_13_out, and_14_out);
  or or_9 (rdMbyp, and_7_out, and_11_out);
  and and_15 (rsMbyp, not_4_out, or_7_out);
endmodule
